// Logisim project alu.circ as structural Verilog
// CAS
module \_8位可控加减法器  (
  input  [7:0] X,
  input  [7:0] Y,
  input  Sub,
  output [7:0] S,
  output Cout,
  output Overflow
);

  wire xor_2_out, xor_3_out, xor_4_out, xor_5_out, xor_6_out, xor_7_out, xor_8_out, xor_9_out,
       \一位全加器fa封装1_1_si , \一位全加器fa封装1_2_cout , \一位全加器fa封装1_3_cout , \一位全加器fa封装1_4_cout , \一位全加器fa封装1_5_cout ,
       \一位全加器fa封装1_6_cout , \一位全加器fa封装1_7_cout , \一位全加器fa封装1_8_cout , \一位全加器fa封装1_9_cout ;
  wire [8:0] \运算指示 ;

  xor xor_1 (Overflow, \一位全加器fa封装1_1_si , S[7]);
  \一位全加器FA封装1  \u_一位全加器fa封装1_1  (
    .Cout(Cout), .Si(\一位全加器fa封装1_1_si ), .Cin(\一位全加器fa封装1_2_cout ), .Xi(X[7]), .Yi(xor_2_out));
  \一位全加器FA封装1  \u_一位全加器fa封装1_2  (
    .Cout(\一位全加器fa封装1_2_cout ), .Si(S[7]), .Cin(\一位全加器fa封装1_3_cout ), .Xi(X[7]), .Yi(xor_2_out));
  xor xor_2 (xor_2_out, Sub, Y[7]);
  \一位全加器FA封装1  \u_一位全加器fa封装1_3  (
    .Cout(\一位全加器fa封装1_3_cout ), .Si(S[6]), .Cin(\一位全加器fa封装1_4_cout ), .Xi(X[6]), .Yi(xor_3_out));
  xor xor_3 (xor_3_out, Sub, Y[6]);
  xor xor_4 (xor_4_out, Sub, Y[5]);
  \一位全加器FA封装1  \u_一位全加器fa封装1_4  (
    .Cout(\一位全加器fa封装1_4_cout ), .Si(S[5]), .Cin(\一位全加器fa封装1_5_cout ), .Xi(X[5]), .Yi(xor_4_out));
  \一位全加器FA封装1  \u_一位全加器fa封装1_5  (
    .Cout(\一位全加器fa封装1_5_cout ), .Si(S[4]), .Cin(\一位全加器fa封装1_6_cout ), .Xi(X[4]), .Yi(xor_5_out));
  xor xor_5 (xor_5_out, Sub, Y[4]);
  \一位全加器FA封装1  \u_一位全加器fa封装1_6  (
    .Cout(\一位全加器fa封装1_6_cout ), .Si(S[3]), .Cin(\一位全加器fa封装1_7_cout ), .Xi(X[3]), .Yi(xor_6_out));
  xor xor_6 (xor_6_out, Sub, Y[3]);
  \一位全加器FA封装1  \u_一位全加器fa封装1_7  (
    .Cout(\一位全加器fa封装1_7_cout ), .Si(S[2]), .Cin(\一位全加器fa封装1_9_cout ), .Xi(X[2]), .Yi(xor_8_out));
  xor xor_7 (xor_7_out, Sub, Y[1]);
  xor xor_8 (xor_8_out, Sub, Y[2]);
  \一位全加器FA封装1  \u_一位全加器fa封装1_8  (.Cout(\一位全加器fa封装1_8_cout ), .Si(S[0]), .Cin(Sub), .Xi(X[0]), .Yi(xor_9_out));
  \一位全加器FA封装1  \u_一位全加器fa封装1_9  (
    .Cout(\一位全加器fa封装1_9_cout ), .Si(S[1]), .Cin(\一位全加器fa封装1_8_cout ), .Xi(X[1]), .Yi(xor_7_out));
  xor xor_9 (xor_9_out, Sub, Y[0]);
  // Probe on X
  // Probe on Y
  // Probe on S
  DotMatrix #(.matrixcols(3), .matrixrows(3)) dotmatrix_1 (.col0(\运算指示 [8:6]), .col1(\运算指示 [5:3]), .col2(\运算指示 [2:0]));
  Multiplexer #(.width(9), .enable("false")) multiplexer_1 (.in0(9'hba), .in1(9'h92), .out(\运算指示 ), .sel(Sub));
  // Probe on X
  // Probe on Y
  // Probe on S

  // Other names for the same wires on the sheet: OF = Overflow

  // Notes on the sheet:
  //   S: pull=down
  //   Y: pull=down
  //   Sub: pull=down
  //   Cout: pull=down
  //   Overflow: pull=down
  //   X: pull=down
  //   8位可控加减法器
  //   输入引脚区
  //   输出引脚区
  //   功能说明：  8位可控加减法器    Sub=0: S = X＋Y  Sub=1:S = X－Y   Cout为最高位进位位，Overflow为有符号溢出标志
  //   =
  //   有符号
  //   =
  //   无符号
endmodule

// CLA74182
module \_4位先行进位74182  (
  input  G4,
  input  P4,
  input  G3,
  input  P3,
  input  G2,
  input  P2,
  input  G1,
  input  P1,
  input  Cin,
  output C4,
  output C3,
  output C2,
  output C1,
  output G_star,
  output P_star
);

  wire and_1_out, and_2_out, and_3_out, and_4_out, and_5_out, and_6_out, and_7_out, and_8_out, and_9_out,
       and_10_out, and_12_out, and_13_out, and_14_out;

  and and_1 (and_1_out, Cin, P1);
  and and_2 (and_2_out, Cin, P1, P2);
  and and_3 (and_3_out, P2, G1);
  and and_4 (and_4_out, Cin, P3, P2, P1);
  and and_5 (and_5_out, P3, G1, P2);
  and and_6 (and_6_out, P3, G2);
  or or_1 (C1, and_1_out, G1);
  or or_2 (C2, and_2_out, and_3_out, G2);
  or or_3 (C3, and_4_out, and_5_out, and_6_out, G3);
  and and_7 (and_7_out, Cin, P4, P3, P2, P1);
  and and_8 (and_8_out, P4, P3, P2, G1);
  and and_9 (and_9_out, P4, P3, G2);
  and and_10 (and_10_out, P4, G3);
  or or_4 (C4, and_7_out, and_8_out, and_9_out, and_10_out, G4);
  and and_11 (P_star, P1, P2, P3, P4);
  and and_12 (and_12_out, G3, P4);
  and and_13 (and_13_out, G2, P3, P4);
  and and_14 (and_14_out, G1, P2, P3, P4);
  or or_5 (G_star, G4, and_12_out, and_13_out, and_14_out);

  // Notes on the sheet:
  //   G1: pull=down
  //   G4: pull=down
  //   P4: pull=down
  //   G3: pull=down
  //   P3: pull=down
  //   P2: pull=down
  //   G2: pull=down
  //   P1: pull=down
  //   Cin: pull=down
  //   输入引脚区
  //   请根据以上引脚以及隧道信号设计完成74LS182先行进位电路，尽可能使用多输入逻辑门，并分析电路延迟
  //   http://218.5.241.24:8018/C35/Course/ZCYL-HB/WLKJ/jy/Chap02/2.6.1.htm
  //   输出引脚区
endmodule

// 4位快速加法器
module \_4位快速加法器  (
  input  [3:0] X,
  input  [3:0] Y,
  input  Cin,
  output [3:0] S,
  output Cout,
  output Cn_1,
  output G_star,
  output P_star
);

  wire _0, _1, _2, _3, and_1_out, and_2_out, and_3_out, and_4_out, \n4位先行进位74182_1_c1 , \n4位先行进位74182_1_c2 ;

  \_4位先行进位74182  \u_4位先行进位74182_1  (
    .G4(and_1_out), .P4(_3), .G3(and_2_out), .P3(_2), .G2(and_3_out), .P2(_1), .G1(and_4_out), .P1(_0),
    .Cin(Cin), .C4(Cout), .C3(Cn_1), .C2(\n4位先行进位74182_1_c2 ), .C1(\n4位先行进位74182_1_c1 ), .G_star(G_star),
    .P_star(P_star));
  and and_1 (and_1_out, X[3], Y[3]);
  xor xor_1 (S[3], Cn_1, _3);
  xor xor_2 (_3, X[3], Y[3]);
  and and_2 (and_2_out, X[2], Y[2]);
  xor xor_3 (_2, X[2], Y[2]);
  xor xor_4 (S[2], \n4位先行进位74182_1_c2 , _2);
  and and_3 (and_3_out, X[1], Y[1]);
  xor xor_5 (_1, X[1], Y[1]);
  xor xor_6 (S[1], \n4位先行进位74182_1_c1 , _1);
  xor xor_7 (S[0], Cin, _0);
  and and_4 (and_4_out, X[0], Y[0]);
  // Probe on X
  // Probe on Y
  // Probe on S
  xor xor_8 (_0, X[0], Y[0]);
  // Probe on X
  // Probe on Y
  // Probe on S

  // Notes on the sheet:
  //   Cin: pull=down
  //   Y: pull=down
  //   X: pull=down
  //   输入引脚区
  //   4位快速加法器
  //   输出引脚区
  //   功能说明:4位Adder  S=X+Y，Cout、Cin分别为最高位、次高位进位位，Cin为进位输入， G* P*为成组进位生成传递函数
  //   +
  //   =
  //   有符号加法
  //   +
  //   =
  //   无符号加法
endmodule

// 16位快速加法器
module \_16位快速加法器  (
  input  [15:0] X,
  input  [15:0] Y,
  input  Cin,
  output Cout,
  output Cn_1,
  output G_star,
  output P_star,
  output [15:0] S
);

  wire C4, C8, C12, \n4位快速加法器_1_g_star , \n4位快速加法器_1_p_star , \n4位快速加法器_2_g_star , \n4位快速加法器_2_p_star ,
       \n4位快速加法器_3_g_star , \n4位快速加法器_3_p_star , \n4位快速加法器_4_g_star , \n4位快速加法器_4_p_star ;

  \_4位先行进位74182  \u_4位先行进位74182_1  (
    .G4(\n4位快速加法器_1_g_star ), .P4(\n4位快速加法器_1_p_star ), .G3(\n4位快速加法器_2_g_star ), .P3(\n4位快速加法器_2_p_star ),
    .G2(\n4位快速加法器_3_g_star ), .P2(\n4位快速加法器_3_p_star ), .G1(\n4位快速加法器_4_g_star ), .P1(\n4位快速加法器_4_p_star ),
    .Cin(Cin), .C4(Cout), .C3(C12), .C2(C8), .C1(C4), .G_star(G_star), .P_star(P_star));
  \_4位快速加法器  \u_4位快速加法器_1  (
    .X(X[15:12]), .Y(Y[15:12]), .Cin(C12), .S(S[15:12]), .G_star(\n4位快速加法器_1_g_star ),
    .P_star(\n4位快速加法器_1_p_star ), .Cn_1(Cn_1));  // open: Cout
  \_4位快速加法器  \u_4位快速加法器_2  (
    .X(X[11:8]), .Y(Y[11:8]), .Cin(C8), .S(S[11:8]), .G_star(\n4位快速加法器_2_g_star ),
    .P_star(\n4位快速加法器_2_p_star ));  // open: Cout, Cn_1
  \_4位快速加法器  \u_4位快速加法器_3  (
    .X(X[7:4]), .Y(Y[7:4]), .Cin(C4), .S(S[7:4]), .G_star(\n4位快速加法器_3_g_star ), .P_star(\n4位快速加法器_3_p_star ));  // open: Cout, Cn_1
  // Probe on X
  // Probe on Y
  // Probe on S
  \_4位快速加法器  \u_4位快速加法器_4  (
    .X(X[3:0]), .Y(Y[3:0]), .Cin(Cin), .S(S[3:0]), .G_star(\n4位快速加法器_4_g_star ), .P_star(\n4位快速加法器_4_p_star ));  // open: Cout, Cn_1
  // Probe on X
  // Probe on Y
  // Probe on S

  // Other names for the same wires on the sheet: S0[3:0] = S[3:0]; S1[3:0] = S[7:4]; S2[3:0] = S[11:8];
  //   S3[3:0] = S[15:12]; X0[3:0] = X[3:0]; X1[3:0] = X[7:4]; X2[3:0] = X[11:8]; X3[3:0] = X[15:12]; Y0[3:0] = Y[3:0];
  //   Y1[3:0] = Y[7:4]; Y2[3:0] = Y[11:8]; Y3[3:0] = Y[15:12]

  // Notes on the sheet:
  //   X: pull=down
  //   Y: pull=down
  //   Cin: pull=down
  //   输入引脚区
  //   16位快速加法器
  //   输出引脚区
  //   功能说明：16位Adder  S=X＋Y，Cout、Cin分别为最高位、次高位进位位，Cin为进位输入， G* P*为成组进位生成传递函数
  //   +
  //   =
  //   有符号加法
  //   +
  //   =
  //   无符号加法
endmodule

// 32位加法器
module \_32位快速加法器  (
  input  Cin,
  input  [31:0] X,
  input  [31:0] Y,
  output Cout,
  output Cn_1,
  output [31:0] S
);

  wire C1, C2, C3, C5, C6, C7, \n4位先行进位74182_2_c4 , \n4位快速加法器_1_g_star , \n4位快速加法器_1_p_star ,
       \n4位快速加法器_2_g_star , \n4位快速加法器_2_p_star , \n4位快速加法器_3_g_star , \n4位快速加法器_3_p_star ,
       \n4位快速加法器_4_g_star , \n4位快速加法器_4_p_star , \n4位快速加法器_5_g_star , \n4位快速加法器_5_p_star ,
       \n4位快速加法器_6_g_star , \n4位快速加法器_6_p_star , \n4位快速加法器_7_g_star , \n4位快速加法器_7_p_star ,
       \n4位快速加法器_8_g_star , \n4位快速加法器_8_p_star ;

  \_4位先行进位74182  \u_4位先行进位74182_1  (
    .G4(\n4位快速加法器_1_g_star ), .P4(\n4位快速加法器_1_p_star ), .G3(\n4位快速加法器_2_g_star ), .P3(\n4位快速加法器_2_p_star ),
    .G2(\n4位快速加法器_3_g_star ), .P2(\n4位快速加法器_3_p_star ), .G1(\n4位快速加法器_4_g_star ), .P1(\n4位快速加法器_4_p_star ),
    .Cin(\n4位先行进位74182_2_c4 ), .C4(Cout), .C3(C7), .C2(C6), .C1(C5));  // open: G_star, P_star
  \_4位快速加法器  \u_4位快速加法器_1  (
    .X(X[31:28]), .Y(Y[31:28]), .Cin(C7), .S(S[31:28]), .G_star(\n4位快速加法器_1_g_star ),
    .P_star(\n4位快速加法器_1_p_star ), .Cn_1(Cn_1));  // open: Cout
  \_4位快速加法器  \u_4位快速加法器_2  (
    .X(X[27:24]), .Y(Y[27:24]), .Cin(C6), .S(S[27:24]), .G_star(\n4位快速加法器_2_g_star ),
    .P_star(\n4位快速加法器_2_p_star ));  // open: Cout, Cn_1
  \_4位快速加法器  \u_4位快速加法器_3  (
    .X(X[23:20]), .Y(Y[23:20]), .Cin(C5), .S(S[23:20]), .G_star(\n4位快速加法器_3_g_star ),
    .P_star(\n4位快速加法器_3_p_star ));  // open: Cout, Cn_1
  // Probe on X
  // Probe on Y
  // Probe on S
  \_4位快速加法器  \u_4位快速加法器_4  (
    .X(X[19:16]), .Y(Y[19:16]), .Cin(\n4位先行进位74182_2_c4 ), .S(S[19:16]), .G_star(\n4位快速加法器_4_g_star ),
    .P_star(\n4位快速加法器_4_p_star ));  // open: Cout, Cn_1
  \_4位先行进位74182  \u_4位先行进位74182_2  (
    .G4(\n4位快速加法器_5_g_star ), .P4(\n4位快速加法器_5_p_star ), .G3(\n4位快速加法器_6_g_star ), .P3(\n4位快速加法器_6_p_star ),
    .G2(\n4位快速加法器_7_g_star ), .P2(\n4位快速加法器_7_p_star ), .G1(\n4位快速加法器_8_g_star ), .P1(\n4位快速加法器_8_p_star ),
    .Cin(Cin), .C4(\n4位先行进位74182_2_c4 ), .C3(C3), .C2(C2), .C1(C1));  // open: G_star, P_star
  // Probe on X
  // Probe on Y
  // Probe on S
  \_4位快速加法器  \u_4位快速加法器_5  (
    .X(X[15:12]), .Y(Y[15:12]), .Cin(C3), .S(S[15:12]), .G_star(\n4位快速加法器_5_g_star ),
    .P_star(\n4位快速加法器_5_p_star ));  // open: Cout, Cn_1
  \_4位快速加法器  \u_4位快速加法器_6  (
    .X(X[11:8]), .Y(Y[11:8]), .Cin(C2), .S(S[11:8]), .G_star(\n4位快速加法器_6_g_star ),
    .P_star(\n4位快速加法器_6_p_star ));  // open: Cout, Cn_1
  \_4位快速加法器  \u_4位快速加法器_7  (
    .X(X[7:4]), .Y(Y[7:4]), .Cin(C1), .S(S[7:4]), .G_star(\n4位快速加法器_7_g_star ), .P_star(\n4位快速加法器_7_p_star ));  // open: Cout, Cn_1
  \_4位快速加法器  \u_4位快速加法器_8  (
    .X(X[3:0]), .Y(Y[3:0]), .Cin(Cin), .S(S[3:0]), .G_star(\n4位快速加法器_8_g_star ), .P_star(\n4位快速加法器_8_p_star ));  // open: Cout, Cn_1

  // Other names for the same wires on the sheet: S0[3:0] = S[3:0]; S1[3:0] = S[7:4]; S2[3:0] = S[11:8];
  //   S3[3:0] = S[15:12]; S4[3:0] = S[19:16]; S5[3:0] = S[23:20]; S6[3:0] = S[27:24]; S7[3:0] = S[31:28];
  //   X0[3:0] = X[3:0]; X1[3:0] = X[7:4]; X2[3:0] = X[11:8]; X3[3:0] = X[15:12]; X4[3:0] = X[19:16];
  //   X5[3:0] = X[23:20]; X6[3:0] = X[27:24]; X7[3:0] = X[31:28]; Y0[3:0] = Y[3:0]; Y1[3:0] = Y[7:4];
  //   Y2[3:0] = Y[11:8]; Y3[3:0] = Y[15:12]; Y4[3:0] = Y[19:16]; Y5[3:0] = Y[23:20]; Y6[3:0] = Y[27:24];
  //   Y7[3:0] = Y[31:28]

  // Notes on the sheet:
  //   Y: pull=down
  //   Cin: pull=down
  //   X: pull=down
  //   输入引脚区
  //   32位快速加法器
  //   功能说明：利用已完成的74182以及4位快速加法器构建速度最快的32位加法器 S = X ＋ Y，并分析电路延迟；
  //   输出引脚区
  //   +
  //   =
  //   有符号加法
  //   +
  //   =
  //   无符号加法
  //   Cout、Cn-1分别为最高位、次高位进位位，Cin为进位输入
endmodule

// 5位阵列乘法器
module \_5位阵列乘法器  (
  input  [4:0] X,
  input  [4:0] Y,
  output [9:0] \乘积 
);

  wire X0Y1, X0Y2, X0Y3, X0Y4, X1Y0, X1Y1, X1Y2, X1Y3, X1Y4, X2Y0, X2Y1, X2Y2, X2Y3, X2Y4, X3Y0, X3Y1, X3Y2,
       X3Y3, X3Y4, X4Y0, X4Y1, X4Y2, X4Y3, X4Y4, \一位全加器fa封装3_2_cout , \一位全加器fa封装3_2_si , \一位全加器fa封装3_3_cout ,
       \一位全加器fa封装3_4_cout , \一位全加器fa封装3_4_si , \一位全加器fa封装3_5_cout , \一位全加器fa封装3_5_si , \一位全加器fa封装3_6_cout ,
       \一位全加器fa封装3_7_cout , \一位全加器fa封装3_7_si , \一位全加器fa封装3_8_cout , \一位全加器fa封装3_8_si , \一位全加器fa封装3_9_cout ,
       \一位全加器fa封装3_9_si , \一位全加器fa封装3_10_cout , \一位全加器fa封装3_11_cout , \一位全加器fa封装3_11_si ,
       \一位全加器fa封装3_12_cout , \一位全加器fa封装3_12_si , \一位全加器fa封装3_13_cout , \一位全加器fa封装3_13_si ,
       \一位全加器fa封装3_14_cout , \一位全加器fa封装3_15_cout , \一位全加器fa封装3_15_si , \一位全加器fa封装3_16_cout ,
       \一位全加器fa封装3_16_si , \一位全加器fa封装3_17_cout , \一位全加器fa封装3_18_cout , \一位全加器fa封装3_18_si ,
       \一位全加器fa封装3_19_cout , \一位全加器fa封装3_20_cout ;

  \一位全加器FA封装3  \u_一位全加器fa封装3_1  (
    .Cout(\乘积 [9]), .Si(\乘积 [8]), .Cin(\一位全加器fa封装3_2_cout ), .Xi(\一位全加器fa封装3_3_cout ), .Yi(X4Y4));
  // Probe on X
  \一位全加器FA封装3  \u_一位全加器fa封装3_2  (
    .Cout(\一位全加器fa封装3_2_cout ), .Si(\一位全加器fa封装3_2_si ), .Cin(\一位全加器fa封装3_4_cout ), .Xi(X3Y4), .Yi(X4Y3));
  \一位全加器FA封装3  \u_一位全加器fa封装3_3  (
    .Cout(\一位全加器fa封装3_3_cout ), .Si(\乘积 [7]), .Cin(\一位全加器fa封装3_5_cout ), .Xi(\一位全加器fa封装3_6_cout ),
    .Yi(\一位全加器fa封装3_2_si ));
  \一位全加器FA封装3  \u_一位全加器fa封装3_4  (
    .Cout(\一位全加器fa封装3_4_cout ), .Si(\一位全加器fa封装3_4_si ), .Cin(\一位全加器fa封装3_7_cout ), .Xi(X3Y3), .Yi(X4Y2));
  \一位全加器FA封装3  \u_一位全加器fa封装3_5  (
    .Cout(\一位全加器fa封装3_5_cout ), .Si(\一位全加器fa封装3_5_si ), .Cin(\一位全加器fa封装3_8_cout ), .Xi(X2Y4),
    .Yi(\一位全加器fa封装3_4_si ));
  \一位全加器FA封装3  \u_一位全加器fa封装3_6  (
    .Cout(\一位全加器fa封装3_6_cout ), .Si(\乘积 [6]), .Cin(\一位全加器fa封装3_9_cout ), .Xi(\一位全加器fa封装3_10_cout ),
    .Yi(\一位全加器fa封装3_5_si ));
  // Probe on Y
  \一位全加器FA封装3  \u_一位全加器fa封装3_7  (
    .Cout(\一位全加器fa封装3_7_cout ), .Si(\一位全加器fa封装3_7_si ), .Cin(\一位全加器fa封装3_11_cout ), .Xi(X3Y2), .Yi(X4Y1));
  \一位全加器FA封装3  \u_一位全加器fa封装3_8  (
    .Cout(\一位全加器fa封装3_8_cout ), .Si(\一位全加器fa封装3_8_si ), .Cin(\一位全加器fa封装3_12_cout ), .Xi(X2Y3),
    .Yi(\一位全加器fa封装3_7_si ));
  \一位全加器FA封装3  \u_一位全加器fa封装3_9  (
    .Cout(\一位全加器fa封装3_9_cout ), .Si(\一位全加器fa封装3_9_si ), .Cin(\一位全加器fa封装3_13_cout ), .Xi(X1Y4),
    .Yi(\一位全加器fa封装3_8_si ));
  \一位全加器FA封装3  \u_一位全加器fa封装3_10  (
    .Cout(\一位全加器fa封装3_10_cout ), .Si(\乘积 [5]), .Cin(\一位全加器fa封装3_14_cout ), .Xi(1'b0), .Yi(\一位全加器fa封装3_9_si ));
  \一位全加器FA封装3  \u_一位全加器fa封装3_11  (
    .Cout(\一位全加器fa封装3_11_cout ), .Si(\一位全加器fa封装3_11_si ), .Cin(1'b0), .Xi(X3Y1), .Yi(X4Y0));
  \一位全加器FA封装3  \u_一位全加器fa封装3_12  (
    .Cout(\一位全加器fa封装3_12_cout ), .Si(\一位全加器fa封装3_12_si ), .Cin(\一位全加器fa封装3_15_cout ), .Xi(X2Y2),
    .Yi(\一位全加器fa封装3_11_si ));
  \一位全加器FA封装3  \u_一位全加器fa封装3_13  (
    .Cout(\一位全加器fa封装3_13_cout ), .Si(\一位全加器fa封装3_13_si ), .Cin(\一位全加器fa封装3_16_cout ), .Xi(X1Y3),
    .Yi(\一位全加器fa封装3_12_si ));
  \一位全加器FA封装3  \u_一位全加器fa封装3_14  (
    .Cout(\一位全加器fa封装3_14_cout ), .Si(\乘积 [4]), .Cin(\一位全加器fa封装3_17_cout ), .Xi(X0Y4), .Yi(\一位全加器fa封装3_13_si ));
  \一位全加器FA封装3  \u_一位全加器fa封装3_15  (
    .Cout(\一位全加器fa封装3_15_cout ), .Si(\一位全加器fa封装3_15_si ), .Cin(1'b0), .Xi(X2Y1), .Yi(X3Y0));
  \一位全加器FA封装3  \u_一位全加器fa封装3_16  (
    .Cout(\一位全加器fa封装3_16_cout ), .Si(\一位全加器fa封装3_16_si ), .Cin(\一位全加器fa封装3_18_cout ), .Xi(X1Y2),
    .Yi(\一位全加器fa封装3_15_si ));
  \一位全加器FA封装3  \u_一位全加器fa封装3_17  (
    .Cout(\一位全加器fa封装3_17_cout ), .Si(\乘积 [3]), .Cin(\一位全加器fa封装3_19_cout ), .Xi(X0Y3), .Yi(\一位全加器fa封装3_16_si ));
  \一位全加器FA封装3  \u_一位全加器fa封装3_18  (
    .Cout(\一位全加器fa封装3_18_cout ), .Si(\一位全加器fa封装3_18_si ), .Cin(1'b0), .Xi(X1Y1), .Yi(X2Y0));
  \一位全加器FA封装3  \u_一位全加器fa封装3_19  (
    .Cout(\一位全加器fa封装3_19_cout ), .Si(\乘积 [2]), .Cin(\一位全加器fa封装3_20_cout ), .Xi(X0Y2), .Yi(\一位全加器fa封装3_18_si ));
  // Probe on X
  // Probe on Y
  // Probe on \乘积 
  \一位全加器FA封装3  \u_一位全加器fa封装3_20  (.Cout(\一位全加器fa封装3_20_cout ), .Si(\乘积 [1]), .Cin(1'b0), .Xi(X0Y1), .Yi(X1Y0));
  \_5位乘法与门阵列  \u_5位乘法与门阵列_1  (
    .X(X), .XY4({X4Y4, X3Y4, X2Y4, X1Y4, X0Y4}), .XY3({X4Y3, X3Y3, X2Y3, X1Y3, X0Y3}),
    .XY2({X4Y2, X3Y2, X2Y2, X1Y2, X0Y2}), .XY1({X4Y1, X3Y1, X2Y1, X1Y1, X0Y1}),
    .XY0({X4Y0, X3Y0, X2Y0, X1Y0, \乘积 [0]}), .Y(Y));

  // Other names for the same wires on the sheet: P[9:0] = \乘积 ; P1 = \乘积 [1]; P2 = \乘积 [2]; P3 = \乘积 [3];
  //   P4 = \乘积 [4]; P5 = \乘积 [5]; P6 = \乘积 [6]; P7 = \乘积 [7]; P8 = \乘积 [8]; P9 = \乘积 [9]; P0 = \乘积 [0];
  //   X0Y0 = \乘积 [0]; XY0[4:0] = {X4Y0, X3Y0, X2Y0, X1Y0, \乘积 [0]}; XY1[4:0] = {X4Y1, X3Y1, X2Y1, X1Y1, X0Y1};
  //   XY2[4:0] = {X4Y2, X3Y2, X2Y2, X1Y2, X0Y2}; XY3[4:0] = {X4Y3, X3Y3, X2Y3, X1Y3, X0Y3};
  //   XY4[4:0] = {X4Y4, X3Y4, X2Y4, X1Y4, X0Y4}

  // Notes on the sheet:
  //   X: pull=down
  //   Y: pull=down
  //   5位无符号阵列乘法器
  //   输入引脚区
  //   功能说明：利用一位全加器构成5位×5位的无符号数阵列乘法器，乘积=X×Y，并分析电路延迟；
  //   输出引脚区
  //   ×
  //   =
endmodule

module \_6位补码阵列乘法器  (
  input  [5:0] X,
  input  [5:0] Y,
  output [10:0] \乘积 
);

  wire [4:0] X_t, Y_t;
  wire [5:0] negator_1_out, negator_3_out;
  wire [9:0] negator_2_out, P9_0_t;

  \_5位阵列乘法器  \u_5位阵列乘法器_1  (.\乘积 (P9_0_t), .X(X_t), .Y(Y_t));
  // Probe on P9_0_t
  // Probe on P9_0_t
  // Probe on X
  // Probe on negator_1_out
  Negator #(.width(6)) negator_1 (.in(X), .out(negator_1_out));
  // Probe on negator_1_out
  xor xor_1 (\乘积 [10], X[5], Y[5]);
  // Probe on Y
  // Probe on X_t
  Multiplexer #(.width(5), .enable("false")) multiplexer_1 (
    .in0(X[4:0]), .in1(negator_1_out[4:0]), .out(X_t), .sel(X[5]));
  // Probe on X_t
  Negator #(.width(10)) negator_2 (.in(P9_0_t), .out(negator_2_out));
  // Probe on negator_3_out
  Negator #(.width(6)) negator_3 (.in(Y), .out(negator_3_out));
  // Probe on negator_3_out
  Multiplexer #(.width(10), .enable("false")) multiplexer_2 (
    .in0(P9_0_t), .in1(negator_2_out), .out(\乘积 [9:0]), .sel(\乘积 [10]));
  // Probe on negator_2_out
  // Probe on negator_2_out
  Multiplexer #(.width(5), .enable("false")) multiplexer_3 (
    .in0(Y[4:0]), .in1(negator_3_out[4:0]), .out(Y_t), .sel(Y[5]));
  // Probe on Y_t
  // Probe on Y_t
  // Probe on X
  // Probe on Y
  // Probe on \乘积 

  // Other names for the same wires on the sheet: P[10:0] = \乘积 ; P0 = \乘积 [0]; P9_0[9:0] = \乘积 [9:0]; P1 = \乘积 [1];
  //   P2 = \乘积 [2]; P3 = \乘积 [3]; P4 = \乘积 [4]; P5 = \乘积 [5]; P6 = \乘积 [6]; P7 = \乘积 [7]; P8 = \乘积 [8]; P9 = \乘积 [9];
  //   P10 = \乘积 [10]; Pf符号位 = \乘积 [10]; X4_0[4:0] = X[4:0]; Y4_0[4:0] = Y[4:0]

  // Notes on the sheet:
  //   6位补码阵列乘法器
  //   输入引脚区
  //   功能说明：利用五位阵列乘法器6位×6位的补码阵列乘法器，乘积P = X × Y，尝试计算 －32 × 1，分析结果  
  //   输出引脚区
  //   ×
  //   =
endmodule

module \原码一位乘法器  (
  input  [7:0] X,
  input  [7:0] Y,
  output [15:0] \乘积 
);

  wire en, RST, \时钟_out ;
  wire [3:0] counter;
  wire [6:0] \n8位串行加法器_1_s ;
  wire [7:0] multiplexer_1_out, multiplexer_2_out;
  wire [7:7] \移位后的Y ;

  Counter #(.width(4), .max('h9), .ongoal("stay")) counter_1 (
    .Q(counter), .clk(\时钟_out ), .clr(RST));  // open: load, D, count, carry
  Clock \u_时钟  (.out(\时钟_out ));
  Multiplexer #(.select(4), .width(8), .enable("false")) multiplexer_1 (
    .in0(Y), .in1({\移位后的Y [7], \乘积 [7:1]}), .in2({\移位后的Y [7], \乘积 [7:1]}), .in3({\移位后的Y [7], \乘积 [7:1]}),
    .in4({\移位后的Y [7], \乘积 [7:1]}), .in5({\移位后的Y [7], \乘积 [7:1]}), .in6({\移位后的Y [7], \乘积 [7:1]}),
    .in7({\移位后的Y [7], \乘积 [7:1]}), .in8({\移位后的Y [7], \乘积 [7:1]}), .in9({\移位后的Y [7], \乘积 [7:1]}),
    .in10({\移位后的Y [7], \乘积 [7:1]}), .in11({\移位后的Y [7], \乘积 [7:1]}), .in12({\移位后的Y [7], \乘积 [7:1]}),
    .in13({\移位后的Y [7], \乘积 [7:1]}), .in14({\移位后的Y [7], \乘积 [7:1]}), .in15({\移位后的Y [7], \乘积 [7:1]}),
    .out(multiplexer_1_out), .sel(counter));
  nand nand_1 (en, counter[0], ~counter[1], ~counter[2], counter[3]);  // NAND_Gate
  Button \u_复位  (.out(RST));
  // Probe on \乘积 [15:8]
  Register register_1 (.D({1'b0, \n8位串行加法器_1_s }), .en(en), .Q(\乘积 [15:8]), .clk(\时钟_out ), .clr(RST));
  \_8位串行加法器  \u_8位串行加法器_1  (
    .X(\乘积 [15:8]), .Y(multiplexer_2_out), .S({\n8位串行加法器_1_s , \移位后的Y [7]}));  // open: Cin, Cout, Overflow
  Register u_Y (.D(multiplexer_1_out), .en(en), .Q(\乘积 [7:0]), .clk(\时钟_out ), .clr(RST));
  // Probe on \乘积 [7:0]
  Multiplexer #(.width(8), .enable("false")) multiplexer_2 (
    .in0({8{1'b0}}), .in1(X), .out(multiplexer_2_out), .sel(\乘积 [0]));
  // Probe on X
  // Probe on Y
  // Probe on \乘积 

  // Other names for the same wires on the sheet: tunnel[7:0] = \乘积 [15:8]; 移位后的Y[6:0] = \乘积 [7:1]

  // Notes on the sheet:
  //   8位无符号一位乘法器
  //   功能说明: 原码一位乘法器   乘积=X*Y，要求采用原码一位乘法实现，最终结果能输出在乘积引脚上
  //   ∑
  //   逻辑右移一位
  //   ∑+Yn|X|
  //   后续所有实验中凡是涉及存储器件，如寄存器、计数器、RAM等，必须增加统一的复位信号RST，方便系统复位
  //   输入输出引脚区
  //   ×
  //   =
  //   核心算法：{ ∑ , Y } = { ∑ ＋ Y  |X|  , Y  } / 2
  //   n
  //   https://blog.csdn.net/kai8wei/article/details/44308557
endmodule

module \补码一位乘法器  (
  input  [7:0] X,
  input  [7:0] Y,
  output [15:0] \乘积 
);

  wire clock_1_out, en, multiplexer_2_out, RST, Yn_1;
  wire [3:0] counter;
  wire [7:0] multiplexer_1_out, multiplexer_3_out, \n8位串行加法器_1_s , not_1_out;
  wire [7:7] \移位后的Y ;

  Clock clock_1 (.out(clock_1_out));
  Counter #(.width(4), .max('h9), .ongoal("stay")) counter_1 (
    .Q(counter), .clk(clock_1_out), .clr(RST));  // open: load, D, count, carry
  Multiplexer #(.select(4), .width(8), .enable("false")) multiplexer_1 (
    .in0(Y), .in1({\移位后的Y [7], \乘积 [7:1]}), .in2({\移位后的Y [7], \乘积 [7:1]}), .in3({\移位后的Y [7], \乘积 [7:1]}),
    .in4({\移位后的Y [7], \乘积 [7:1]}), .in5({\移位后的Y [7], \乘积 [7:1]}), .in6({\移位后的Y [7], \乘积 [7:1]}),
    .in7({\移位后的Y [7], \乘积 [7:1]}), .in8({\移位后的Y [7], \乘积 [7:1]}), .in9({\移位后的Y [7], \乘积 [7:1]}),
    .in10({\移位后的Y [7], \乘积 [7:1]}), .in11({\移位后的Y [7], \乘积 [7:1]}), .in12({\移位后的Y [7], \乘积 [7:1]}),
    .in13({\移位后的Y [7], \乘积 [7:1]}), .in14({\移位后的Y [7], \乘积 [7:1]}), .in15({\移位后的Y [7], \乘积 [7:1]}),
    .out(multiplexer_1_out), .sel(counter));
  nand nand_1 (en, counter[0], ~counter[1], ~counter[2], counter[3]);  // NAND_Gate
  Button \u_复位  (.out(RST));
  Register register (
    .D({{2{\n8位串行加法器_1_s [7]}}, \n8位串行加法器_1_s [5:0]}), .en(en), .Q(\乘积 [15:8]), .clk(clock_1_out), .clr(RST));
  \_8位串行加法器  \u_8位串行加法器_1  (
    .X(\乘积 [15:8]), .Y(multiplexer_3_out), .Cin(multiplexer_2_out),
    .S({\n8位串行加法器_1_s [7], \n8位串行加法器_1_s [5:0], \移位后的Y [7]}));  // open: Cout, Overflow
  Multiplexer #(.select(2), .enable("false")) multiplexer_2 (
    .in0(1'b0), .in1(1'b0), .in2(1'b1), .in3(1'b0), .out(multiplexer_2_out), .sel({\乘积 [0], Yn_1}));
  // Probe on multiplexer_3_out
  // Probe on \乘积 [15:8]
  Multiplexer #(.select(2), .width(8), .enable("false")) multiplexer_3 (
    .in0({8{1'b0}}), .in1(X), .in2(not_1_out), .in3({8{1'b0}}), .out(multiplexer_3_out), .sel({\乘积 [0], Yn_1}));
  Register u_Y (.D(multiplexer_1_out), .en(en), .Q(\乘积 [7:0]), .clk(clock_1_out), .clr(RST));
  // Probe on \乘积 [7:0]
  // Probe on {\乘积 [0], Yn_1}
  assign not_1_out = ~X;  // NOT_Gate not_1, 8 bits wide
  // Probe on X
  // Probe on not_1_out
  // Probe on X
  // Probe on Y
  // Probe on \乘积 
  // Probe on Yn_1
  Register #(.width(1)) Yn_1_2 (.D(\乘积 [0]), .en(en), .Q(Yn_1), .clk(clock_1_out), .clr(RST));

  // Other names for the same wires on the sheet: Yn = \乘积 [0]; tunnel[7:0] = \乘积 [15:8]; 移位后的Y[6:0] = \乘积 [7:1]

  // Notes on the sheet:
  //   8位补码 Booth一位乘法器
  //   功能说明: 补码一位乘法器   乘积=X×Y，要求采用补码一位乘法实现，最终结果能输出在乘积引脚上
  //   算术右移一位
  //   ∑+ (Yn+1-Yn)补
  //   后续所有实验中凡是涉及存储器件，如寄存器、计数器、RAM等，必须增加统一的复位信号RST，方便系统复位
  //   输入输出引脚区
  //   核心算法：{ ∑,Y } = { ∑ ＋（Y      －  Y  ）[X]   , Y } / 2
  //   ×
  //   =
  //   n
  //   n+1
  //   补
endmodule

// ALU
module \算术逻辑运算单元ALU  (
  input  [31:0] X,
  input  [31:0] Y,
  input  [3:0] AluOP,
  output Signed_Overflow,
  output UnSigned_Overflow,
  output Equal,
  output [31:0] Result,
  output [31:0] Result_2
);

  wire and_2_out, and_3_out, and_4_out, and_5_out, comparator_1_lt, comparator_2_lt, \n32位快速加法器_2_cout ,
       not_3_out, not_4_out, not_5_out, not_6_out, not_7_out, not_8_out, OFADD, OFSUB, UOFADD, UOFSUB;
  wire [31:0] not_2_out, resultADD, resultAND, resultARS, resultCMPS, resultCMPUS, resultDivQ, resultDivR,
       resultLLS, resultLRS, resultMulHigh, resultMulLow, resultNOR, resultOR, resultSUB, resultXOR;

  // Probe on X
  // Probe on X
  not not_1 (UOFSUB, \n32位快速加法器_2_cout );
  // Probe on Y
  // Probe on Y
  \_32位快速加法器  \u_32位快速加法器_1  (.X(X), .Y(Y), .Cin(1'b0), .S(resultADD), .Cout(UOFADD));  // open: Cn_1
  \_32位快速加法器  \u_32位快速加法器_2  (
    .X(X), .Y(not_2_out), .Cin(1'b1), .S(resultSUB), .Cout(\n32位快速加法器_2_cout ));  // open: Cn_1
  assign not_2_out = ~Y;  // NOT_Gate not_2, 32 bits wide
  assign resultAND = X & Y;  // AND_Gate and_1, 32 bits wide
  assign resultOR = X | Y;  // OR_Gate or_1, 32 bits wide
  assign resultXOR = X ^ Y;  // XOR_Gate xor_1, 32 bits wide
  assign resultNOR = ~(X | Y);  // NOR_Gate nor_1, 32 bits wide
  Multiplexer #(.select(4), .enable("false")) multiplexer_1 (
    .in0(1'b0), .in1(1'b0), .in2(1'b0), .in3(1'b0), .in4(1'b0), .in5(OFADD), .in6(OFSUB), .in7(1'b0),
    .in8(1'b0), .in9(1'b0), .in10(1'b0), .in11(1'b0), .in12(1'b0), .in13(1'b0), .in14(1'b0), .in15(1'b0),
    .out(Signed_Overflow), .sel(AluOP));
  Shifter #(.width(32)) shifter_1 (.in(X), .\dist (Y[4:0]), .out(resultLLS));
  Shifter #(.width(32), .shift("ar")) shifter_2 (.in(X), .\dist (Y[4:0]), .out(resultARS));
  Shifter #(.width(32), .shift("lr")) shifter_3 (.in(X), .\dist (Y[4:0]), .out(resultLRS));
  // Probe on AluOP
  Multiplexer #(.select(4), .width(32), .enable("false")) multiplexer_2 (
    .in0(resultLLS), .in1(resultARS), .in2(resultLRS), .in3(resultMulLow), .in4(resultDivQ), .in5(resultADD),
    .in6(resultSUB), .in7(resultAND), .in8(resultOR), .in9(resultXOR), .in10(resultNOR), .in11(resultCMPS),
    .in12(resultCMPUS), .in13({32{1'b0}}), .in14({32{1'b0}}), .in15({32{1'b0}}), .out(Result), .sel(AluOP));
  // Probe on Result
  // Probe on Result
  not not_3 (not_3_out, X[31]);
  not not_4 (not_4_out, Y[31]);
  not not_5 (not_5_out, resultADD[31]);
  not not_6 (not_6_out, X[31]);
  not not_7 (not_7_out, resultSUB[31]);
  not not_8 (not_8_out, Y[31]);
  Multiplexer #(.select(4), .enable("false")) multiplexer_3 (
    .in0(1'b0), .in1(1'b0), .in2(1'b0), .in3(1'b0), .in4(1'b0), .in5(UOFADD), .in6(UOFSUB), .in7(1'b0),
    .in8(1'b0), .in9(1'b0), .in10(1'b0), .in11(1'b0), .in12(1'b0), .in13(1'b0), .in14(1'b0), .in15(1'b0),
    .out(UnSigned_Overflow), .sel(AluOP));
  // Probe on Result_2
  and and_2 (and_2_out, not_3_out, resultADD[31], not_4_out);
  and and_3 (and_3_out, X[31], not_5_out, Y[31]);
  and and_4 (and_4_out, not_6_out, resultSUB[31], Y[31]);
  and and_5 (and_5_out, X[31], not_7_out, not_8_out);
  Multiplexer #(.width(32), .enable("false")) multiplexer_4 (
    .in0({32{1'b0}}), .in1(32'h1), .out(resultCMPUS), .sel(comparator_1_lt));
  Comparator #(.width(32), .mode("unsigned")) comparator_1 (.a(X), .b(Y), .lt(comparator_1_lt));  // open: gt, eq
  Comparator #(.width(32)) comparator_2 (.a(X), .b(Y), .lt(comparator_2_lt));  // open: gt, eq
  Multiplier #(.width(32)) multiplier_1 (.a(X), .b(Y), .out(resultMulLow), .cin({32{1'b0}}), .cout(resultMulHigh));
  Divider #(.width(32)) divider_1 (.a(X), .b(Y), .out(resultDivQ), .upper({32{1'b0}}), .rem(resultDivR));
  or or_2 (OFADD, and_2_out, and_3_out);
  or or_3 (OFSUB, and_4_out, and_5_out);
  Multiplexer #(.width(32), .enable("false")) multiplexer_5 (
    .in0({32{1'b0}}), .in1(32'h1), .out(resultCMPS), .sel(comparator_2_lt));
  Multiplexer #(.select(4), .width(32), .enable("false")) multiplexer_6 (
    .in0({32{1'b0}}), .in1({32{1'b0}}), .in2({32{1'b0}}), .in3(resultMulHigh), .in4(resultDivR),
    .in5({32{1'b0}}), .in6({32{1'b0}}), .in7({32{1'b0}}), .in8({32{1'b0}}), .in9({32{1'b0}}),
    .in10({32{1'b0}}), .in11({32{1'b0}}), .in12({32{1'b0}}), .in13({32{1'b0}}), .in14({32{1'b0}}),
    .in15({32{1'b0}}), .out(Result_2), .sel(AluOP));
  Comparator #(.width(32), .mode("unsigned")) comparator_3 (.a(X), .b(Y), .eq(Equal));  // open: gt, lt

  // Other names for the same wires on the sheet: OF = Signed_Overflow; Result2[31:0] = Result_2; S[3:0] = AluOP;
  //   UOF = UnSigned_Overflow

  // Notes on the sheet:
  //   X: pull=down
  //   AluOP: pull=down
  //   Y: pull=down
  //   32位MIPS运算器
  //   不要改变此引脚区域内容，也不要改变ALU封装形式
  //   输入引脚
  //   请在下方利用上方输入输出引脚的隧道信号构建ALU电路，ctrl+d复制选择部件
  //   华中科技大学计算机学院 计算机组成原理，鸣谢加州大学伯克利CS61C课程
  //   输出引脚
  //   探测区域
endmodule

module \ALU自动测试  (
  output [7:0] Test_num,
  output Equal
);

  wire ADD, AND, and_1_out, CF, CF_S, CLK, comparator_2_eq, comparator_3_eq, DIV, \EQ__标志 , EQ_OK, EQ_S,
       Halt, MUL, multiplexer_1_out, NEQ, nHalt, NOR, OF, OF_OK, OR, priority_encoder_1_gs, ROK, SAR, SCMP,
       SLL, SLR, SUB, tunnel, UCMP, UOF_OK, XOR, \与 , \乘法 , \减法 , \加法 , \异或 , \悬空检测 , \或 , \或非 , \无符号比较 ,
       \无符号溢出标志 , \有符号比较 , \有符号溢出标志 , \算术右移 , \逻辑右移 , \逻辑左移 , \除法 ;
  wire [2:2] FLAG_Standard;
  wire [3:0] ALUOP, High, Low, Mid;
  wire [7:0] adder_1_out, \单项评分_1_total , \单项评分_1_扣分 , \单项评分_1_正确条数 , \单项评分_2_total , \单项评分_2_扣分 ,
       \单项评分_2_正确条数 , \单项评分_3_total , \单项评分_3_扣分 , \单项评分_3_正确条数 , \单项评分_4_total , \单项评分_4_扣分 , \单项评分_4_正确条数 ,
       \单项评分_5_total , \单项评分_5_扣分 , \单项评分_5_正确条数 , \单项评分_6_total , \单项评分_6_扣分 , \单项评分_6_正确条数 ,
       \单项评分_7_total , \单项评分_7_扣分 , \单项评分_7_正确条数 , \单项评分_8_total , \单项评分_8_扣分 , \单项评分_8_正确条数 ,
       \单项评分_9_total , \单项评分_9_扣分 , \单项评分_9_正确条数 , \单项评分_10_total , \单项评分_10_扣分 , \单项评分_10_正确条数 ,
       \单项评分_11_total , \单项评分_11_扣分 , \单项评分_11_正确条数 , \单项评分_12_total , \单项评分_12_扣分 , \单项评分_12_正确条数 ,
       \单项评分_13_total , \单项评分_13_扣分 , \单项评分_13_正确条数 , \单项评分_14_total , \单项评分_14_扣分 , \单项评分_14_正确条数 ,
       \单项评分_15_total , \单项评分_15_扣分 , \单项评分_15_正确条数 , \单项评分_16_total , \单项评分_16_扣分 , \单项评分_16_正确条数 ,
       \总评分_result ;
  wire [9:0] counter_1_q;
  wire [31:0] bit_extender_1_out, R, R2, R2_Standard, R_Standard, X, Y;

  Clock clock_1 (.out(CLK));
  Register register_1 (.D(adder_1_out), .en(nHalt), .Q(Test_num), .clk(CLK));  // open: clr
  LED \u_测试完成  (.in(Halt));
  Counter #(.width(10), .max('h3ff)) counter_1 (
    .count(NEQ), .Q(counter_1_q), .clk(CLK), .clr(Halt));  // open: load, D, carry
  LED #(.active("false")) led_1 (.in(\逻辑左移 ));
  LED #(.active("false")) led_2 (.in(\逻辑右移 ));
  LED #(.active("false")) led_3 (.in(\EQ__标志 ));
  \单项评分  \u_单项评分_1  (
    .EQ(ROK), .EN(nHalt), .\分值 (5'b00101), .CLK(CLK), .\正确条数 (\单项评分_1_正确条数 ), .\扣分 (\单项评分_1_扣分 ),
    .Right(\逻辑左移 ), .ALU_SWITCH(SLL), .Total(\单项评分_1_total ));
  // Probe on \单项评分_1_total 
  // Probe on \单项评分_1_正确条数 
  // Probe on \单项评分_1_扣分 
  Adder adder_1 (.a(8'h1), .b(Test_num), .out(adder_1_out));  // open: cin, cout
  not not_1 (nHalt, Halt);
  Comparator #(.width(4)) comparator_1 (.a(ALUOP), .b(4'b1111), .eq(Halt));  // open: gt, lt
  and and_1 (and_1_out, ~Halt, NEQ);  // AND_Gate
  LED #(.active("false")) led_4 (.in(\算术右移 ));
  LED led_5 (.in(\悬空检测 ));
  \单项评分  \u_单项评分_2  (
    .EQ(ROK), .EN(nHalt), .\分值 (5'b00101), .CLK(CLK), .\正确条数 (\单项评分_2_正确条数 ), .\扣分 (\单项评分_2_扣分 ),
    .Right(\算术右移 ), .ALU_SWITCH(SAR), .Total(\单项评分_2_total ));
  // Probe on \单项评分_3_total 
  // Probe on \单项评分_2_total 
  // Probe on \单项评分_2_正确条数 
  // Probe on \单项评分_2_扣分 
  trace trace_1 (
    .in_1(Test_num), .X(X), .Y(Y), .AluOP(ALUOP), .R(R_Standard), .R2(R2_Standard),
    .FLAGS({FLAG_Standard[2], CF_S, EQ_S}));
  RAM #(.addrWidth(10), .dataWidth(32), .bus("separate")) ram_1 (
    .addr(counter_1_q), .din(X), .str(and_1_out), .clk(CLK));  // open: data, sel, ld, clr
  LED #(.active("false")) led_6 (.in(\与 ));
  LED #(.active("false")) led_7 (.in(\或 ));
  LED #(.active("false")) led_8 (.in(\有符号溢出标志 ));
  \单项评分  \u_单项评分_3  (
    .EQ(ROK), .EN(nHalt), .\分值 (5'b00101), .CLK(CLK), .\正确条数 (\单项评分_3_正确条数 ), .\扣分 (\单项评分_3_扣分 ),
    .Right(\逻辑右移 ), .ALU_SWITCH(SLR), .Total(\单项评分_3_total ));
  // Probe on \单项评分_4_total 
  // Probe on \单项评分_3_正确条数 
  // Probe on \单项评分_4_正确条数 
  // Probe on \单项评分_3_扣分 
  \单项评分  \u_单项评分_4  (
    .EQ(ROK), .EN(nHalt), .\分值 (5'b00101), .CLK(CLK), .\正确条数 (\单项评分_4_正确条数 ), .\扣分 (\单项评分_4_扣分 ),
    .Right(\乘法 ), .ALU_SWITCH(MUL), .Total(\单项评分_4_total ));
  // Probe on \单项评分_6_total 
  // Probe on \单项评分_6_正确条数 
  // Probe on \单项评分_6_扣分 
  // Probe on \单项评分_4_扣分 
  RAM #(.addrWidth(10), .dataWidth(32), .bus("separate")) ram_2 (
    .addr(counter_1_q), .din(Y), .str(and_1_out), .clk(CLK));  // open: data, sel, ld, clr
  assign bit_extender_1_out = {{28{1'b0}}, ALUOP};  // Bit_Extender bit_extender_1
  LED #(.active("false")) led_9 (.in(\或非 ));
  LED #(.active("false")) led_10 (.in(\异或 ));
  \单项评分  \u_单项评分_5  (
    .EQ(ROK), .EN(nHalt), .\分值 (5'b00101), .CLK(CLK), .\正确条数 (\单项评分_5_正确条数 ), .\扣分 (\单项评分_5_扣分 ),
    .Right(\加法 ), .ALU_SWITCH(ADD), .Total(\单项评分_5_total ));
  \单项评分  \u_单项评分_6  (
    .EQ(ROK), .EN(nHalt), .\分值 (5'b00101), .CLK(CLK), .\正确条数 (\单项评分_6_正确条数 ), .\扣分 (\单项评分_6_扣分 ),
    .Right(\除法 ), .ALU_SWITCH(DIV), .Total(\单项评分_6_total ));
  // Probe on \单项评分_5_total 
  // Probe on \单项评分_5_正确条数 
  // Probe on \单项评分_5_扣分 
  \算术逻辑运算单元ALU  \u_算术逻辑运算单元alu_1  (
    .AluOP(ALUOP), .X(X), .Equal(Equal), .Result(R), .Signed_Overflow(OF), .Y(Y), .Result_2(R2),
    .UnSigned_Overflow(CF));
  LED #(.active("false")) led_11 (.in(\乘法 ));
  LED #(.active("false")) led_12 (.in(\除法 ));
  LED #(.active("false")) led_13 (.in(\无符号溢出标志 ));
  \单项评分  \u_单项评分_7  (
    .EQ(ROK), .EN(nHalt), .\分值 (5'b00101), .CLK(CLK), .\正确条数 (\单项评分_7_正确条数 ), .\扣分 (\单项评分_7_扣分 ),
    .Right(\减法 ), .ALU_SWITCH(SUB), .Total(\单项评分_7_total ));
  // Probe on \单项评分_7_total 
  // Probe on \单项评分_7_正确条数 
  // Probe on \单项评分_7_扣分 
  RAM #(.addrWidth(10), .dataWidth(32), .bus("separate")) ram_3 (
    .addr(counter_1_q), .din(bit_extender_1_out), .str(and_1_out), .clk(CLK));  // open: data, sel, ld, clr
  LED #(.active("false")) led_14 (.in(\加法 ));
  LED #(.active("false")) led_15 (.in(\减法 ));
  \单项评分  \u_单项评分_8  (
    .EQ(ROK), .EN(nHalt), .\分值 (5'b00101), .CLK(CLK), .\正确条数 (\单项评分_8_正确条数 ), .\扣分 (\单项评分_8_扣分 ),
    .Right(\与 ), .ALU_SWITCH(AND), .Total(\单项评分_8_total ));
  // Probe on \单项评分_8_total 
  // Probe on \单项评分_8_正确条数 
  // Probe on \单项评分_8_扣分 
  \总评分  \u_总评分  (
    .in_1(\单项评分_1_扣分 ), .in_2(\单项评分_2_扣分 ), .in_3(\单项评分_3_扣分 ), .in_4(\单项评分_4_扣分 ), .in_5(\单项评分_6_扣分 ),
    .in_6(\单项评分_5_扣分 ), .in_7(\单项评分_7_扣分 ), .in_8(\单项评分_8_扣分 ), .in_9(\单项评分_9_扣分 ), .in_10(\单项评分_10_扣分 ),
    .in_11(\单项评分_11_扣分 ), .in_12(\单项评分_12_扣分 ), .in_13(\单项评分_13_扣分 ), .in_14(\单项评分_14_扣分 ),
    .in_15(\单项评分_15_扣分 ), .in_16(\单项评分_16_扣分 ), .\悬空扣分 (\悬空检测 ), .Result(\总评分_result ), .High(High),
    .Low(Low), .Mid(Mid));
  Hex_Digit_Display hex_digit_display_1 (.value(High));  // open: dp
  Hex_Digit_Display hex_digit_display_2 (.value(Mid));  // open: dp
  \单项评分  \u_单项评分_9  (
    .EQ(ROK), .EN(nHalt), .\分值 (5'b00101), .CLK(CLK), .\正确条数 (\单项评分_9_正确条数 ), .\扣分 (\单项评分_9_扣分 ),
    .Right(\或 ), .ALU_SWITCH(OR), .Total(\单项评分_9_total ));
  // Probe on nothing
  // Probe on \单项评分_9_正确条数 
  // Probe on \单项评分_9_扣分 
  // Probe on \总评分_result 
  Hex_Digit_Display hex_digit_display_3 (.value(Low));  // open: dp
  LED #(.active("false")) led_16 (.in(\有符号比较 ));
  LED #(.active("false")) led_17 (.in(\无符号比较 ));
  \单项评分  \u_单项评分_10  (
    .EQ(ROK), .EN(nHalt), .\分值 (5'b00101), .CLK(CLK), .\正确条数 (\单项评分_10_正确条数 ), .\扣分 (\单项评分_10_扣分 ),
    .Right(\异或 ), .ALU_SWITCH(XOR), .Total(\单项评分_10_total ));
  // Probe on \单项评分_10_total 
  // Probe on \单项评分_11_total 
  // Probe on \单项评分_10_正确条数 
  // Probe on \单项评分_10_扣分 
  \单项评分  \u_单项评分_11  (
    .EQ(ROK), .EN(nHalt), .\分值 (5'b00101), .CLK(CLK), .\正确条数 (\单项评分_11_正确条数 ), .\扣分 (\单项评分_11_扣分 ),
    .Right(\或非 ), .ALU_SWITCH(NOR), .Total(\单项评分_11_total ));
  // Probe on \单项评分_12_total 
  // Probe on \单项评分_12_正确条数 
  // Probe on \单项评分_11_正确条数 
  // Probe on \单项评分_11_扣分 
  \单项评分  \u_单项评分_12  (
    .EQ(ROK), .EN(nHalt), .\分值 (5'b00101), .CLK(CLK), .\正确条数 (\单项评分_12_正确条数 ), .\扣分 (\单项评分_12_扣分 ),
    .Right(\有符号比较 ), .ALU_SWITCH(SCMP), .Total(\单项评分_12_total ));
  // Probe on \单项评分_13_total 
  // Probe on \单项评分_13_正确条数 
  // Probe on \单项评分_13_扣分 
  // Probe on \单项评分_12_扣分 
  \单项评分  \u_单项评分_13  (
    .EQ(ROK), .EN(nHalt), .\分值 (5'b00101), .CLK(CLK), .\正确条数 (\单项评分_13_正确条数 ), .\扣分 (\单项评分_13_扣分 ),
    .Right(\无符号比较 ), .ALU_SWITCH(UCMP), .Total(\单项评分_13_total ));
  \单项评分  \u_单项评分_14  (
    .EQ(EQ_OK), .EN(nHalt), .\分值 (5'b01000), .CLK(CLK), .\正确条数 (\单项评分_14_正确条数 ), .\扣分 (\单项评分_14_扣分 ),
    .Right(\EQ__标志 ), .ALU_SWITCH(EQ_OK), .Total(\单项评分_14_total ));
  // Probe on \单项评分_14_total 
  // Probe on \单项评分_14_正确条数 
  // Probe on \单项评分_14_扣分 
  \单项评分  \u_单项评分_15  (
    .EQ(OF_OK), .EN(nHalt), .\分值 (5'b01000), .CLK(CLK), .\正确条数 (\单项评分_15_正确条数 ), .\扣分 (\单项评分_15_扣分 ),
    .Right(\有符号溢出标志 ), .ALU_SWITCH(1'b1), .Total(\单项评分_15_total ));
  // Probe on \单项评分_15_total 
  // Probe on \单项评分_15_正确条数 
  // Probe on \单项评分_15_扣分 
  \单项评分  \u_单项评分_16  (
    .EQ(UOF_OK), .EN(nHalt), .\分值 (5'b01000), .CLK(CLK), .\正确条数 (\单项评分_16_正确条数 ), .\扣分 (\单项评分_16_扣分 ),
    .Right(\无符号溢出标志 ), .ALU_SWITCH(1'b1), .Total(\单项评分_16_total ));
  // Probe on \单项评分_16_total 
  // Probe on \单项评分_16_正确条数 
  // Probe on \单项评分_16_扣分 
  // Probe on ALUOP
  Decoder #(.select(4), .enable("false")) decoder_1 (
    .out0(SLL), .out1(SAR), .out2(SLR), .out3(MUL), .out4(DIV), .out5(ADD), .out6(SUB), .out7(AND),
    .out8(OR), .out9(XOR), .out10(NOR), .out11(SCMP), .out12(UCMP), .sel(ALUOP));  // open: out13, out14, out15
  xnor xnor_1 (EQ_OK, EQ_S, Equal);
  xnor xnor_2 (OF_OK, FLAG_Standard[2], OF);
  xnor xnor_3 (UOF_OK, CF_S, CF);
  Comparator #(.width(32)) comparator_2 (.a(R_Standard), .b(R), .eq(comparator_2_eq));  // open: gt, lt
  Comparator #(.width(32)) comparator_3 (.a(R2_Standard), .b(R2), .eq(comparator_3_eq));  // open: gt, lt
  Multiplexer #(.disabled(0), .enable("false")) multiplexer_1 (
    .in0(1'b1), .in1(1'b1), .out(multiplexer_1_out), .sel(CF));
  and and_2 (ROK, comparator_2_eq, comparator_3_eq);
  or or_1 (tunnel, ADD, SUB);
  Priority_Encoder #(.select(1)) priority_encoder_1 (
    .in0(multiplexer_1_out), .in1(multiplexer_1_out), .gs(priority_encoder_1_gs));  // open: out, en_out, en_in
  not not_2 (\悬空检测 , priority_encoder_1_gs);
  nand nand_1 (NEQ, EQ_OK, OF_OK, UOF_OK, ROK);

  // Other names for the same wires on the sheet: EQ = Equal; FLAG_Standard[1:0] = {CF_S, EQ_S};
  //   OF_S = FLAG_Standard[2]

  // Notes on the sheet:
  //   操作码为F停止
  //   错误记录X
  //   错误记录Y
  //   运算故障指示灯，红色异常
  //   错误记录ALUOP
  //   3个存储器存储的是所有错误的测试用例
  //   错误扣分值
  //   成绩
  //   ctrl+K驱动时钟自动测试
  //   华中科技大学：计算机组成课程组
  //   悬空扣5分
  //   错误扣分值
  //   各部分分值
  //   各部分扣分
  //   悬空检测
endmodule

// 与门阵列
module \_5位乘法与门阵列  (
  input  [4:0] X,
  input  [4:0] Y,
  output [4:0] XY0,
  output [4:0] XY1,
  output [4:0] XY2,
  output [4:0] XY3,
  output [4:0] XY4
);

  and and_1 (XY0[4], X[4], Y[0]);
  and and_2 (XY1[4], X[4], Y[1]);
  and and_3 (XY2[4], X[4], Y[2]);
  and and_4 (XY3[4], X[4], Y[3]);
  and and_5 (XY4[4], X[4], Y[4]);
  and and_6 (XY0[3], X[3], Y[0]);
  and and_7 (XY1[3], X[3], Y[1]);
  and and_8 (XY2[3], X[3], Y[2]);
  and and_9 (XY3[3], X[3], Y[3]);
  and and_10 (XY4[3], X[3], Y[4]);
  and and_11 (XY0[2], X[2], Y[0]);
  and and_12 (XY1[2], X[2], Y[1]);
  and and_13 (XY2[2], X[2], Y[2]);
  and and_14 (XY3[2], X[2], Y[3]);
  and and_15 (XY4[2], X[2], Y[4]);
  and and_16 (XY0[0], X[0], Y[0]);
  and and_17 (XY0[1], X[1], Y[0]);
  and and_18 (XY1[1], X[1], Y[1]);
  and and_19 (XY1[0], X[0], Y[1]);
  and and_20 (XY2[0], X[0], Y[2]);
  and and_21 (XY2[1], X[1], Y[2]);
  and and_22 (XY3[1], X[1], Y[3]);
  and and_23 (XY3[0], X[0], Y[3]);
  and and_24 (XY4[1], X[1], Y[4]);
  and and_25 (XY4[0], X[0], Y[4]);

  // Other names for the same wires on the sheet: X0Y0 = XY0[0]; X1Y0 = XY0[1]; X2Y0 = XY0[2]; X3Y0 = XY0[3];
  //   X4Y0 = XY0[4]; X0Y1 = XY1[0]; X1Y1 = XY1[1]; X2Y1 = XY1[2]; X3Y1 = XY1[3]; X4Y1 = XY1[4]; X0Y2 = XY2[0];
  //   X1Y2 = XY2[1]; X2Y2 = XY2[2]; X3Y2 = XY2[3]; X4Y2 = XY2[4]; X0Y3 = XY3[0]; X1Y3 = XY3[1]; X2Y3 = XY3[2];
  //   X3Y3 = XY3[3]; X4Y3 = XY3[4]; X0Y4 = XY4[0]; X1Y4 = XY4[1]; X2Y4 = XY4[2]; X3Y4 = XY4[3]; X4Y4 = XY4[4]
endmodule

// FA
module \一位全加器FA封装1  (
  input  Cin,
  input  Xi,
  input  Yi,
  output Cout,
  output Si
);

  wire AND_2_out, AND_out, XOR_2_out;

  or OR (Cout, AND_out, AND_2_out);
  and AND (AND_out, Xi, Yi);
  and AND_2 (AND_2_out, Cin, XOR_2_out);
  xor XOR (Si, Cin, XOR_2_out);
  xor XOR_2 (XOR_2_out, Xi, Yi);

  // Notes on the sheet:
  //   Cin: pull=down
  //   Yi: pull=down
  //   Xi: pull=down
  //   Si = Xi ^ Yi ^ Cin
  //   Cout = Xi Yi + Cin (Xi ^ Yi)
endmodule

module \一位全加器FA封装2  (
  input  Cin,
  input  Xi,
  input  Yi,
  output Cout,
  output Si
);

  wire AND_2_out, AND_out, XOR_2_out;

  or OR (Cout, AND_out, AND_2_out);
  and AND (AND_out, Xi, Yi);
  and AND_2 (AND_2_out, Cin, XOR_2_out);
  xor XOR (Si, Cin, XOR_2_out);
  xor XOR_2 (XOR_2_out, Xi, Yi);

  // Notes on the sheet:
  //   Si = Xi ^ Yi ^ Cin
  //   Cout = Xi Yi + Cin (Xi ^ Yi)
endmodule

module \一位全加器FA封装3  (
  input  Cin,
  input  Xi,
  input  Yi,
  output Cout,
  output Si
);

  wire AND_2_out, AND_out, XOR_2_out;

  or OR (Cout, AND_out, AND_2_out);
  and AND (AND_out, Xi, Yi);
  and AND_2 (AND_2_out, Cin, XOR_2_out);
  xor XOR (Si, Cin, XOR_2_out);
  xor XOR_2 (XOR_2_out, Xi, Yi);

  // Notes on the sheet:
  //   Si = Xi ^ Yi ^ Cin
  //   Cout = Xi Yi + Cin (Xi ^ Yi)
endmodule

module \_8位串行加法器  (
  input  [7:0] X,
  input  [7:0] Y,
  input  Cin,
  output [7:0] S,
  output Cout,
  output Overflow
);

  wire \一位全加器fa封装1_2_cout , \一位全加器fa封装1_3_cout , \一位全加器fa封装1_4_cout , \一位全加器fa封装1_5_cout ,
       \一位全加器fa封装1_6_cout , \一位全加器fa封装1_7_cout , \一位全加器fa封装1_8_cout ;

  xor xor_1 (Overflow, Cout, \一位全加器fa封装1_2_cout );
  \一位全加器FA封装1  \u_一位全加器fa封装1_1  (.Cout(Cout), .Si(S[7]), .Cin(\一位全加器fa封装1_2_cout ), .Xi(X[7]), .Yi(Y[7]));
  \一位全加器FA封装1  \u_一位全加器fa封装1_2  (
    .Cout(\一位全加器fa封装1_2_cout ), .Si(S[6]), .Cin(\一位全加器fa封装1_3_cout ), .Xi(X[6]), .Yi(Y[6]));
  \一位全加器FA封装1  \u_一位全加器fa封装1_3  (
    .Cout(\一位全加器fa封装1_3_cout ), .Si(S[5]), .Cin(\一位全加器fa封装1_4_cout ), .Xi(X[5]), .Yi(Y[5]));
  \一位全加器FA封装1  \u_一位全加器fa封装1_4  (
    .Cout(\一位全加器fa封装1_4_cout ), .Si(S[4]), .Cin(\一位全加器fa封装1_5_cout ), .Xi(X[4]), .Yi(Y[4]));
  \一位全加器FA封装1  \u_一位全加器fa封装1_5  (
    .Cout(\一位全加器fa封装1_5_cout ), .Si(S[3]), .Cin(\一位全加器fa封装1_6_cout ), .Xi(X[3]), .Yi(Y[3]));
  \一位全加器FA封装1  \u_一位全加器fa封装1_6  (
    .Cout(\一位全加器fa封装1_6_cout ), .Si(S[2]), .Cin(\一位全加器fa封装1_7_cout ), .Xi(X[2]), .Yi(Y[2]));
  // Probe on X
  // Probe on Y
  // Probe on S
  \一位全加器FA封装1  \u_一位全加器fa封装1_7  (
    .Cout(\一位全加器fa封装1_7_cout ), .Si(S[1]), .Cin(\一位全加器fa封装1_8_cout ), .Xi(X[1]), .Yi(Y[1]));
  // Probe on X
  // Probe on Y
  // Probe on S
  \一位全加器FA封装1  \u_一位全加器fa封装1_8  (.Cout(\一位全加器fa封装1_8_cout ), .Si(S[0]), .Cin(Cin), .Xi(X[0]), .Yi(Y[0]));

  // Other names for the same wires on the sheet: OF = Overflow

  // Notes on the sheet:
  //   Cin: pull=down
  //   X: pull=down
  //   Y: pull=down
  //   输入引脚区
  //   符号位
  //   输出引脚区
  //   +
  //   =
  //   有符号加法
  //   +
  //   =
  //   无符号加法
endmodule

module \华莱士树  (
);

  wire undriven, undriven_2, undriven_3, undriven_4, undriven_5, undriven_6, undriven_7, undriven_8,
       undriven_9, undriven_10, undriven_11, undriven_12, undriven_13, undriven_14, undriven_15, undriven_16,
       undriven_17, undriven_18, undriven_19, undriven_20, undriven_21, undriven_22, undriven_23,
       undriven_24, undriven_25, undriven_26, undriven_27, undriven_28, undriven_29, undriven_30,
       undriven_31, undriven_32, undriven_33, undriven_34, undriven_35, undriven_36, undriven_37,
       undriven_38, undriven_39, undriven_40, undriven_41, undriven_42, undriven_43, undriven_44,
       undriven_45, undriven_46, undriven_47, undriven_48, undriven_49, undriven_50, undriven_51,
       undriven_52, undriven_53, undriven_54, undriven_55, undriven_56, undriven_57, undriven_58,
       undriven_59, undriven_60, undriven_61, undriven_62, undriven_63, undriven_64, undriven_65,
       undriven_66, undriven_67, undriven_68, undriven_69, undriven_70, undriven_71, undriven_72,
       undriven_73, undriven_74, undriven_75, undriven_76, undriven_77, undriven_78, undriven_79,
       undriven_80, undriven_81, undriven_82, undriven_83, undriven_84, undriven_85, undriven_86,
       undriven_87, undriven_88, undriven_89, undriven_90, undriven_91, undriven_92, undriven_93,
       undriven_94, undriven_95, undriven_96, undriven_97, undriven_98, undriven_99, undriven_100,
       undriven_101, undriven_102, undriven_103, undriven_104, undriven_105, undriven_106, undriven_107,
       undriven_108, undriven_109, undriven_110, undriven_111, undriven_112, undriven_113, undriven_114,
       undriven_115, undriven_116, undriven_117, undriven_118, undriven_119, undriven_120, undriven_121,
       undriven_122, undriven_123, undriven_124, undriven_125, undriven_126, undriven_127, undriven_128,
       undriven_130, \一位全加器fa封装2_1_cout , \一位全加器fa封装2_1_si , \一位全加器fa封装2_2_si , \一位全加器fa封装2_3_cout ,
       \一位全加器fa封装2_3_si , \一位全加器fa封装2_4_si , \一位全加器fa封装2_5_si , \一位全加器fa封装2_6_si , \一位全加器fa封装2_7_si ,
       \一位全加器fa封装2_8_si , \一位全加器fa封装2_9_cout , \一位全加器fa封装2_9_si , \一位全加器fa封装2_10_si , \一位全加器fa封装2_11_si ,
       \一位全加器fa封装2_12_cout , \一位全加器fa封装2_12_si , \一位全加器fa封装2_13_si , \一位全加器fa封装2_14_si ,
       \一位全加器fa封装2_15_cout , \一位全加器fa封装2_15_si , \一位全加器fa封装2_16_si , \一位全加器fa封装2_17_cout ,
       \一位全加器fa封装2_17_si , \一位全加器fa封装2_18_si , \一位全加器fa封装2_19_si , \一位全加器fa封装2_20_si , \一位全加器fa封装2_21_si ,
       \一位全加器fa封装2_22_si , \一位全加器fa封装2_23_cout , \一位全加器fa封装2_23_si , \一位全加器fa封装2_24_si ,
       \一位全加器fa封装2_25_cout , \一位全加器fa封装2_25_si , \一位全加器fa封装2_26_si , \一位全加器fa封装2_27_si , \一位全加器fa封装2_28_si ,
       \一位全加器fa封装2_29_cout , \一位全加器fa封装2_29_si , \一位全加器fa封装2_30_si , \一位全加器fa封装2_31_cout ,
       \一位全加器fa封装2_31_si , \一位全加器fa封装2_32_si , \一位全加器fa封装2_33_si , \一位全加器fa封装2_34_si , \一位全加器fa封装2_35_si ,
       \一位全加器fa封装2_36_si , \一位全加器fa封装2_37_cout , \一位全加器fa封装2_37_si , \一位全加器fa封装2_38_si , \一位全加器fa封装2_39_si ,
       \一位全加器fa封装2_40_cout , \一位全加器fa封装2_40_si , \一位全加器fa封装2_41_si , \一位全加器fa封装2_42_si ,
       \一位全加器fa封装2_43_cout , \一位全加器fa封装2_43_si , \一位全加器fa封装2_44_si , \一位全加器fa封装2_45_cout ,
       \一位全加器fa封装2_45_si , \一位全加器fa封装2_46_si , \一位全加器fa封装2_47_si , \一位全加器fa封装2_48_si , \一位全加器fa封装2_49_si ,
       \一位全加器fa封装2_50_si , \一位全加器fa封装2_51_cout , \一位全加器fa封装2_51_si , \一位全加器fa封装2_52_si ,
       \一位全加器fa封装2_53_cout , \一位全加器fa封装2_53_si , \一位全加器fa封装2_54_si , \一位全加器fa封装2_55_si , \一位全加器fa封装2_56_si ,
       \一位全加器fa封装2_57_cout , \一位全加器fa封装2_57_si , \一位全加器fa封装2_58_si , \一位全加器fa封装2_59_cout ,
       \一位全加器fa封装2_59_si , \一位全加器fa封装2_60_si , \一位全加器fa封装2_61_si , \一位全加器fa封装2_62_si , \一位全加器fa封装2_63_si ,
       \一位全加器fa封装2_64_si , \一位全加器fa封装2_65_cout , \一位全加器fa封装2_65_si , \一位全加器fa封装2_66_si ,
       \一位全加器fa封装2_67_cout , \一位全加器fa封装2_67_si , \一位全加器fa封装2_68_si , \一位全加器fa封装2_69_si , \一位全加器fa封装2_70_si ,
       \一位全加器fa封装2_71_cout , \一位全加器fa封装2_71_si , \一位全加器fa封装2_72_si , \一位全加器fa封装2_73_cout ,
       \一位全加器fa封装2_73_si , \一位全加器fa封装2_74_si , \一位全加器fa封装2_75_si , \一位全加器fa封装2_76_si , \一位全加器fa封装2_77_si ,
       \一位全加器fa封装2_78_si , \一位全加器fa封装2_79_cout , \一位全加器fa封装2_79_si , \一位全加器fa封装2_80_si ,
       \一位全加器fa封装2_81_cout , \一位全加器fa封装2_81_si , \一位全加器fa封装2_82_si , \一位全加器fa封装2_83_si , \一位全加器fa封装2_84_si ,
       \一位全加器fa封装2_85_cout , \一位全加器fa封装2_85_si , \一位全加器fa封装2_86_si , \一位全加器fa封装2_87_cout ,
       \一位全加器fa封装2_87_si , \一位全加器fa封装2_88_si , \一位全加器fa封装2_89_si , \一位全加器fa封装2_90_si , \一位全加器fa封装2_91_si ,
       \一位全加器fa封装2_92_si , \一位全加器fa封装2_93_cout , \一位全加器fa封装2_93_si , \一位全加器fa封装2_94_si , \一位全加器fa封装2_95_si ,
       \一位全加器fa封装2_96_cout , \一位全加器fa封装2_96_si , \一位全加器fa封装2_97_si , \一位全加器fa封装2_98_si ,
       \一位全加器fa封装2_99_cout , \一位全加器fa封装2_99_si , \一位全加器fa封装2_100_si , \一位全加器fa封装2_101_cout ,
       \一位全加器fa封装2_101_si , \一位全加器fa封装2_102_si , \一位全加器fa封装2_103_si , \一位全加器fa封装2_104_si ,
       \一位全加器fa封装2_105_si , \一位全加器fa封装2_106_si , \一位全加器fa封装2_107_cout , \一位全加器fa封装2_107_si ,
       \一位全加器fa封装2_108_si , \一位全加器fa封装2_109_cout , \一位全加器fa封装2_109_si , \一位全加器fa封装2_110_si ,
       \一位全加器fa封装2_111_si , \一位全加器fa封装2_112_si ;
  wire [1:0] undriven_131, \一位全加器fa封装2_4_cout , \一位全加器fa封装2_10_cout , \一位全加器fa封装2_16_cout ,
       \一位全加器fa封装2_22_cout , \一位全加器fa封装2_32_cout , \一位全加器fa封装2_38_cout , \一位全加器fa封装2_44_cout ,
       \一位全加器fa封装2_50_cout , \一位全加器fa封装2_60_cout , \一位全加器fa封装2_66_cout , \一位全加器fa封装2_72_cout ,
       \一位全加器fa封装2_78_cout , \一位全加器fa封装2_88_cout , \一位全加器fa封装2_94_cout , \一位全加器fa封装2_100_cout ,
       \一位全加器fa封装2_106_cout ;
  wire [2:0] undriven_129, \一位全加器fa封装2_6_cout , \一位全加器fa封装2_14_cout , \一位全加器fa封装2_21_cout ,
       \一位全加器fa封装2_28_cout , \一位全加器fa封装2_34_cout , \一位全加器fa封装2_42_cout , \一位全加器fa封装2_49_cout ,
       \一位全加器fa封装2_55_cout , \一位全加器fa封装2_63_cout , \一位全加器fa封装2_70_cout , \一位全加器fa封装2_77_cout ,
       \一位全加器fa封装2_83_cout , \一位全加器fa封装2_90_cout , \一位全加器fa封装2_98_cout , \一位全加器fa封装2_105_cout ,
       \一位全加器fa封装2_111_cout ;

  shape shape_1 ();
  \一位全加器FA封装2  \u_一位全加器fa封装2_1  (
    .Cout(\一位全加器fa封装2_1_cout ), .Si(\一位全加器fa封装2_1_si ), .Cin(\一位全加器fa封装2_6_si ), .Xi(\一位全加器fa封装2_2_si ),
    .Yi(\一位全加器fa封装2_7_si ));
  \一位全加器FA封装2  \u_一位全加器fa封装2_2  (
    .Cout(\一位全加器fa封装2_6_cout [2]), .Si(\一位全加器fa封装2_2_si ), .Cin(undriven_3), .Xi(undriven), .Yi(undriven_2));
  \一位全加器FA封装2  \u_一位全加器fa封装2_3  (
    .Cout(\一位全加器fa封装2_3_cout ), .Si(\一位全加器fa封装2_3_si ), .Cin(\一位全加器fa封装2_10_cout [0]),
    .Xi(\一位全加器fa封装2_4_si ), .Yi(\一位全加器fa封装2_10_cout [1]));
  \一位全加器FA封装2  \u_一位全加器fa封装2_4  (
    .Cout(\一位全加器fa封装2_4_cout [0]), .Si(\一位全加器fa封装2_4_si ), .Cin(\一位全加器fa封装2_12_cout ),
    .Xi(\一位全加器fa封装2_1_si ), .Yi(\一位全加器fa封装2_5_si ));
  \一位全加器FA封装2  \u_一位全加器fa封装2_5  (
    .Cout(\一位全加器fa封装2_4_cout [1]), .Si(\一位全加器fa封装2_5_si ), .Cin(\一位全加器fa封装2_14_cout [0]),
    .Xi(\一位全加器fa封装2_14_cout [2]), .Yi(\一位全加器fa封装2_14_cout [1]));
  \一位全加器FA封装2  \u_一位全加器fa封装2_6  (
    .Cout(\一位全加器fa封装2_6_cout [0]), .Si(\一位全加器fa封装2_6_si ), .Cin(1'b0), .Xi(undriven_7), .Yi(undriven_8));
  \一位全加器FA封装2  \u_一位全加器fa封装2_7  (
    .Cout(\一位全加器fa封装2_6_cout [1]), .Si(\一位全加器fa封装2_7_si ), .Cin(undriven_6), .Xi(undriven_4), .Yi(undriven_5));
  \一位全加器FA封装2  \u_一位全加器fa封装2_8  (
    .Cout(\一位全加器fa封装2_14_cout [2]), .Si(\一位全加器fa封装2_8_si ), .Cin(undriven_11), .Xi(undriven_9),
    .Yi(undriven_10));
  \一位全加器FA封装2  \u_一位全加器fa封装2_9  (
    .Cout(\一位全加器fa封装2_9_cout ), .Si(\一位全加器fa封装2_9_si ), .Cin(\一位全加器fa封装2_16_cout [0]),
    .Xi(\一位全加器fa封装2_10_si ), .Yi(\一位全加器fa封装2_16_cout [1]));
  \一位全加器FA封装2  \u_一位全加器fa封装2_10  (
    .Cout(\一位全加器fa封装2_10_cout [0]), .Si(\一位全加器fa封装2_10_si ), .Cin(\一位全加器fa封装2_17_cout ),
    .Xi(\一位全加器fa封装2_12_si ), .Yi(\一位全加器fa封装2_11_si ));
  \一位全加器FA封装2  \u_一位全加器fa封装2_11  (
    .Cout(\一位全加器fa封装2_10_cout [1]), .Si(\一位全加器fa封装2_11_si ), .Cin(\一位全加器fa封装2_21_cout [0]),
    .Xi(\一位全加器fa封装2_21_cout [2]), .Yi(\一位全加器fa封装2_21_cout [1]));
  \一位全加器FA封装2  \u_一位全加器fa封装2_12  (
    .Cout(\一位全加器fa封装2_12_cout ), .Si(\一位全加器fa封装2_12_si ), .Cin(\一位全加器fa封装2_14_si ), .Xi(\一位全加器fa封装2_8_si ),
    .Yi(\一位全加器fa封装2_13_si ));
  \一位全加器FA封装2  \u_一位全加器fa封装2_13  (
    .Cout(\一位全加器fa封装2_14_cout [1]), .Si(\一位全加器fa封装2_13_si ), .Cin(undriven_14), .Xi(undriven_12),
    .Yi(undriven_13));
  shape shape_2 ();
  \一位全加器FA封装2  \u_一位全加器fa封装2_14  (
    .Cout(\一位全加器fa封装2_14_cout [0]), .Si(\一位全加器fa封装2_14_si ), .Cin(1'b0), .Xi(undriven_15), .Yi(undriven_16));
  \一位全加器FA封装2  \u_一位全加器fa封装2_15  (
    .Cout(\一位全加器fa封装2_15_cout ), .Si(\一位全加器fa封装2_15_si ), .Cin(\一位全加器fa封装2_22_cout [0]),
    .Xi(\一位全加器fa封装2_16_si ), .Yi(\一位全加器fa封装2_22_cout [1]));
  \一位全加器FA封装2  \u_一位全加器fa封装2_16  (
    .Cout(\一位全加器fa封装2_16_cout [0]), .Si(\一位全加器fa封装2_16_si ), .Cin(\一位全加器fa封装2_23_cout ),
    .Xi(\一位全加器fa封装2_17_si ), .Yi(\一位全加器fa封装2_20_si ));
  \一位全加器FA封装2  \u_一位全加器fa封装2_17  (
    .Cout(\一位全加器fa封装2_17_cout ), .Si(\一位全加器fa封装2_17_si ), .Cin(\一位全加器fa封装2_21_si ), .Xi(\一位全加器fa封装2_19_si ),
    .Yi(\一位全加器fa封装2_18_si ));
  \一位全加器FA封装2  \u_一位全加器fa封装2_18  (
    .Cout(\一位全加器fa封装2_21_cout [1]), .Si(\一位全加器fa封装2_18_si ), .Cin(undriven_22), .Xi(undriven_20),
    .Yi(undriven_21));
  \一位全加器FA封装2  \u_一位全加器fa封装2_19  (
    .Cout(\一位全加器fa封装2_21_cout [2]), .Si(\一位全加器fa封装2_19_si ), .Cin(undriven_19), .Xi(undriven_17),
    .Yi(undriven_18));
  \一位全加器FA封装2  \u_一位全加器fa封装2_20  (
    .Cout(\一位全加器fa封装2_16_cout [1]), .Si(\一位全加器fa封装2_20_si ), .Cin(\一位全加器fa封装2_28_cout [0]),
    .Xi(\一位全加器fa封装2_28_cout [2]), .Yi(\一位全加器fa封装2_28_cout [1]));
  \一位全加器FA封装2  \u_一位全加器fa封装2_21  (
    .Cout(\一位全加器fa封装2_21_cout [0]), .Si(\一位全加器fa封装2_21_si ), .Cin(1'b0), .Xi(undriven_23), .Yi(undriven_24));
  \一位全加器FA封装2  \u_一位全加器fa封装2_22  (
    .Cout(\一位全加器fa封装2_22_cout [0]), .Si(\一位全加器fa封装2_22_si ), .Cin(\一位全加器fa封装2_29_cout ),
    .Xi(\一位全加器fa封装2_23_si ), .Yi(\一位全加器fa封装2_26_si ));
  \一位全加器FA封装2  \u_一位全加器fa封装2_23  (
    .Cout(\一位全加器fa封装2_23_cout ), .Si(\一位全加器fa封装2_23_si ), .Cin(\一位全加器fa封装2_28_si ), .Xi(\一位全加器fa封装2_24_si ),
    .Yi(\一位全加器fa封装2_27_si ));
  \一位全加器FA封装2  \u_一位全加器fa封装2_24  (
    .Cout(\一位全加器fa封装2_28_cout [2]), .Si(\一位全加器fa封装2_24_si ), .Cin(undriven_27), .Xi(undriven_25),
    .Yi(undriven_26));
  shape shape_3 ();
  \一位全加器FA封装2  \u_一位全加器fa封装2_25  (
    .Cout(\一位全加器fa封装2_25_cout ), .Si(\一位全加器fa封装2_25_si ), .Cin(\一位全加器fa封装2_32_cout [0]),
    .Xi(\一位全加器fa封装2_22_si ), .Yi(\一位全加器fa封装2_32_cout [1]));
  \一位全加器FA封装2  \u_一位全加器fa封装2_26  (
    .Cout(\一位全加器fa封装2_22_cout [1]), .Si(\一位全加器fa封装2_26_si ), .Cin(\一位全加器fa封装2_34_cout [0]),
    .Xi(\一位全加器fa封装2_34_cout [2]), .Yi(\一位全加器fa封装2_34_cout [1]));
  \一位全加器FA封装2  \u_一位全加器fa封装2_27  (
    .Cout(\一位全加器fa封装2_28_cout [1]), .Si(\一位全加器fa封装2_27_si ), .Cin(undriven_30), .Xi(undriven_28),
    .Yi(undriven_29));
  \一位全加器FA封装2  \u_一位全加器fa封装2_28  (
    .Cout(\一位全加器fa封装2_28_cout [0]), .Si(\一位全加器fa封装2_28_si ), .Cin(1'b0), .Xi(undriven_31), .Yi(undriven_32));
  \一位全加器FA封装2  \u_一位全加器fa封装2_29  (
    .Cout(\一位全加器fa封装2_29_cout ), .Si(\一位全加器fa封装2_29_si ), .Cin(\一位全加器fa封装2_34_si ), .Xi(\一位全加器fa封装2_30_si ),
    .Yi(\一位全加器fa封装2_35_si ));
  \一位全加器FA封装2  \u_一位全加器fa封装2_30  (
    .Cout(\一位全加器fa封装2_34_cout [2]), .Si(\一位全加器fa封装2_30_si ), .Cin(undriven_35), .Xi(undriven_33),
    .Yi(undriven_34));
  \一位全加器FA封装2  \u_一位全加器fa封装2_31  (
    .Cout(\一位全加器fa封装2_31_cout ), .Si(\一位全加器fa封装2_31_si ), .Cin(\一位全加器fa封装2_38_cout [0]),
    .Xi(\一位全加器fa封装2_32_si ), .Yi(\一位全加器fa封装2_38_cout [1]));
  \一位全加器FA封装2  \u_一位全加器fa封装2_32  (
    .Cout(\一位全加器fa封装2_32_cout [0]), .Si(\一位全加器fa封装2_32_si ), .Cin(\一位全加器fa封装2_40_cout ),
    .Xi(\一位全加器fa封装2_29_si ), .Yi(\一位全加器fa封装2_33_si ));
  \一位全加器FA封装2  \u_一位全加器fa封装2_33  (
    .Cout(\一位全加器fa封装2_32_cout [1]), .Si(\一位全加器fa封装2_33_si ), .Cin(\一位全加器fa封装2_42_cout [0]),
    .Xi(\一位全加器fa封装2_42_cout [2]), .Yi(\一位全加器fa封装2_42_cout [1]));
  \一位全加器FA封装2  \u_一位全加器fa封装2_34  (
    .Cout(\一位全加器fa封装2_34_cout [0]), .Si(\一位全加器fa封装2_34_si ), .Cin(1'b0), .Xi(undriven_39), .Yi(undriven_40));
  \一位全加器FA封装2  \u_一位全加器fa封装2_35  (
    .Cout(\一位全加器fa封装2_34_cout [1]), .Si(\一位全加器fa封装2_35_si ), .Cin(undriven_38), .Xi(undriven_36),
    .Yi(undriven_37));
  \一位全加器FA封装2  \u_一位全加器fa封装2_36  (
    .Cout(\一位全加器fa封装2_42_cout [2]), .Si(\一位全加器fa封装2_36_si ), .Cin(undriven_43), .Xi(undriven_41),
    .Yi(undriven_42));
  \一位全加器FA封装2  \u_一位全加器fa封装2_37  (
    .Cout(\一位全加器fa封装2_37_cout ), .Si(\一位全加器fa封装2_37_si ), .Cin(\一位全加器fa封装2_44_cout [0]),
    .Xi(\一位全加器fa封装2_38_si ), .Yi(\一位全加器fa封装2_44_cout [1]));
  \一位全加器FA封装2  \u_一位全加器fa封装2_38  (
    .Cout(\一位全加器fa封装2_38_cout [0]), .Si(\一位全加器fa封装2_38_si ), .Cin(\一位全加器fa封装2_45_cout ),
    .Xi(\一位全加器fa封装2_40_si ), .Yi(\一位全加器fa封装2_39_si ));
  \一位全加器FA封装2  \u_一位全加器fa封装2_39  (
    .Cout(\一位全加器fa封装2_38_cout [1]), .Si(\一位全加器fa封装2_39_si ), .Cin(\一位全加器fa封装2_49_cout [0]),
    .Xi(\一位全加器fa封装2_49_cout [2]), .Yi(\一位全加器fa封装2_49_cout [1]));
  \一位全加器FA封装2  \u_一位全加器fa封装2_40  (
    .Cout(\一位全加器fa封装2_40_cout ), .Si(\一位全加器fa封装2_40_si ), .Cin(\一位全加器fa封装2_42_si ), .Xi(\一位全加器fa封装2_36_si ),
    .Yi(\一位全加器fa封装2_41_si ));
  \一位全加器FA封装2  \u_一位全加器fa封装2_41  (
    .Cout(\一位全加器fa封装2_42_cout [1]), .Si(\一位全加器fa封装2_41_si ), .Cin(undriven_46), .Xi(undriven_44),
    .Yi(undriven_45));
  shape shape_4 ();
  \一位全加器FA封装2  \u_一位全加器fa封装2_42  (
    .Cout(\一位全加器fa封装2_42_cout [0]), .Si(\一位全加器fa封装2_42_si ), .Cin(1'b0), .Xi(undriven_47), .Yi(undriven_48));
  \一位全加器FA封装2  \u_一位全加器fa封装2_43  (
    .Cout(\一位全加器fa封装2_43_cout ), .Si(\一位全加器fa封装2_43_si ), .Cin(\一位全加器fa封装2_50_cout [0]),
    .Xi(\一位全加器fa封装2_44_si ), .Yi(\一位全加器fa封装2_50_cout [1]));
  \一位全加器FA封装2  \u_一位全加器fa封装2_44  (
    .Cout(\一位全加器fa封装2_44_cout [0]), .Si(\一位全加器fa封装2_44_si ), .Cin(\一位全加器fa封装2_51_cout ),
    .Xi(\一位全加器fa封装2_45_si ), .Yi(\一位全加器fa封装2_48_si ));
  \一位全加器FA封装2  \u_一位全加器fa封装2_45  (
    .Cout(\一位全加器fa封装2_45_cout ), .Si(\一位全加器fa封装2_45_si ), .Cin(\一位全加器fa封装2_49_si ), .Xi(\一位全加器fa封装2_46_si ),
    .Yi(\一位全加器fa封装2_47_si ));
  \一位全加器FA封装2  \u_一位全加器fa封装2_46  (
    .Cout(\一位全加器fa封装2_49_cout [2]), .Si(\一位全加器fa封装2_46_si ), .Cin(undriven_51), .Xi(undriven_49),
    .Yi(undriven_50));
  \一位全加器FA封装2  \u_一位全加器fa封装2_47  (
    .Cout(\一位全加器fa封装2_49_cout [1]), .Si(\一位全加器fa封装2_47_si ), .Cin(undriven_54), .Xi(undriven_52),
    .Yi(undriven_53));
  \一位全加器FA封装2  \u_一位全加器fa封装2_48  (
    .Cout(\一位全加器fa封装2_44_cout [1]), .Si(\一位全加器fa封装2_48_si ), .Cin(\一位全加器fa封装2_55_cout [0]),
    .Xi(\一位全加器fa封装2_55_cout [2]), .Yi(\一位全加器fa封装2_55_cout [1]));
  \一位全加器FA封装2  \u_一位全加器fa封装2_49  (
    .Cout(\一位全加器fa封装2_49_cout [0]), .Si(\一位全加器fa封装2_49_si ), .Cin(1'b0), .Xi(undriven_55), .Yi(undriven_56));
  \一位全加器FA封装2  \u_一位全加器fa封装2_50  (
    .Cout(\一位全加器fa封装2_50_cout [0]), .Si(\一位全加器fa封装2_50_si ), .Cin(\一位全加器fa封装2_57_cout ),
    .Xi(\一位全加器fa封装2_51_si ), .Yi(\一位全加器fa封装2_54_si ));
  \一位全加器FA封装2  \u_一位全加器fa封装2_51  (
    .Cout(\一位全加器fa封装2_51_cout ), .Si(\一位全加器fa封装2_51_si ), .Cin(\一位全加器fa封装2_55_si ), .Xi(\一位全加器fa封装2_52_si ),
    .Yi(\一位全加器fa封装2_56_si ));
  \一位全加器FA封装2  \u_一位全加器fa封装2_52  (
    .Cout(\一位全加器fa封装2_55_cout [2]), .Si(\一位全加器fa封装2_52_si ), .Cin(undriven_59), .Xi(undriven_57),
    .Yi(undriven_58));
  shape shape_5 ();
  \一位全加器FA封装2  \u_一位全加器fa封装2_53  (
    .Cout(\一位全加器fa封装2_53_cout ), .Si(\一位全加器fa封装2_53_si ), .Cin(\一位全加器fa封装2_60_cout [0]),
    .Xi(\一位全加器fa封装2_50_si ), .Yi(\一位全加器fa封装2_60_cout [1]));
  \一位全加器FA封装2  \u_一位全加器fa封装2_54  (
    .Cout(\一位全加器fa封装2_50_cout [1]), .Si(\一位全加器fa封装2_54_si ), .Cin(\一位全加器fa封装2_63_cout [0]),
    .Xi(\一位全加器fa封装2_63_cout [2]), .Yi(\一位全加器fa封装2_63_cout [1]));
  \一位全加器FA封装2  \u_一位全加器fa封装2_55  (
    .Cout(\一位全加器fa封装2_55_cout [0]), .Si(\一位全加器fa封装2_55_si ), .Cin(1'b0), .Xi(undriven_63), .Yi(undriven_64));
  \一位全加器FA封装2  \u_一位全加器fa封装2_56  (
    .Cout(\一位全加器fa封装2_55_cout [1]), .Si(\一位全加器fa封装2_56_si ), .Cin(undriven_62), .Xi(undriven_60),
    .Yi(undriven_61));
  \一位全加器FA封装2  \u_一位全加器fa封装2_57  (
    .Cout(\一位全加器fa封装2_57_cout ), .Si(\一位全加器fa封装2_57_si ), .Cin(\一位全加器fa封装2_63_si ), .Xi(\一位全加器fa封装2_58_si ),
    .Yi(\一位全加器fa封装2_62_si ));
  \一位全加器FA封装2  \u_一位全加器fa封装2_58  (
    .Cout(\一位全加器fa封装2_63_cout [2]), .Si(\一位全加器fa封装2_58_si ), .Cin(undriven_67), .Xi(undriven_65),
    .Yi(undriven_66));
  \一位全加器FA封装2  \u_一位全加器fa封装2_59  (
    .Cout(\一位全加器fa封装2_59_cout ), .Si(\一位全加器fa封装2_59_si ), .Cin(\一位全加器fa封装2_66_cout [0]),
    .Xi(\一位全加器fa封装2_60_si ), .Yi(\一位全加器fa封装2_66_cout [1]));
  \一位全加器FA封装2  \u_一位全加器fa封装2_60  (
    .Cout(\一位全加器fa封装2_60_cout [0]), .Si(\一位全加器fa封装2_60_si ), .Cin(\一位全加器fa封装2_67_cout ),
    .Xi(\一位全加器fa封装2_57_si ), .Yi(\一位全加器fa封装2_61_si ));
  \一位全加器FA封装2  \u_一位全加器fa封装2_61  (
    .Cout(\一位全加器fa封装2_60_cout [1]), .Si(\一位全加器fa封装2_61_si ), .Cin(\一位全加器fa封装2_70_cout [0]),
    .Xi(\一位全加器fa封装2_70_cout [2]), .Yi(\一位全加器fa封装2_70_cout [1]));
  \一位全加器FA封装2  \u_一位全加器fa封装2_62  (
    .Cout(\一位全加器fa封装2_63_cout [1]), .Si(\一位全加器fa封装2_62_si ), .Cin(undriven_70), .Xi(undriven_68),
    .Yi(undriven_69));
  \一位全加器FA封装2  \u_一位全加器fa封装2_63  (
    .Cout(\一位全加器fa封装2_63_cout [0]), .Si(\一位全加器fa封装2_63_si ), .Cin(1'b0), .Xi(undriven_71), .Yi(undriven_72));
  \一位全加器FA封装2  \u_一位全加器fa封装2_64  (
    .Cout(\一位全加器fa封装2_70_cout [2]), .Si(\一位全加器fa封装2_64_si ), .Cin(undriven_75), .Xi(undriven_73),
    .Yi(undriven_74));
  \一位全加器FA封装2  \u_一位全加器fa封装2_65  (
    .Cout(\一位全加器fa封装2_65_cout ), .Si(\一位全加器fa封装2_65_si ), .Cin(\一位全加器fa封装2_72_cout [0]),
    .Xi(\一位全加器fa封装2_66_si ), .Yi(\一位全加器fa封装2_72_cout [1]));
  \一位全加器FA封装2  \u_一位全加器fa封装2_66  (
    .Cout(\一位全加器fa封装2_66_cout [0]), .Si(\一位全加器fa封装2_66_si ), .Cin(\一位全加器fa封装2_73_cout ),
    .Xi(\一位全加器fa封装2_67_si ), .Yi(\一位全加器fa封装2_68_si ));
  \一位全加器FA封装2  \u_一位全加器fa封装2_67  (
    .Cout(\一位全加器fa封装2_67_cout ), .Si(\一位全加器fa封装2_67_si ), .Cin(\一位全加器fa封装2_70_si ), .Xi(\一位全加器fa封装2_64_si ),
    .Yi(\一位全加器fa封装2_69_si ));
  \一位全加器FA封装2  \u_一位全加器fa封装2_68  (
    .Cout(\一位全加器fa封装2_66_cout [1]), .Si(\一位全加器fa封装2_68_si ), .Cin(\一位全加器fa封装2_77_cout [0]),
    .Xi(\一位全加器fa封装2_77_cout [2]), .Yi(\一位全加器fa封装2_77_cout [1]));
  \一位全加器FA封装2  \u_一位全加器fa封装2_69  (
    .Cout(\一位全加器fa封装2_70_cout [1]), .Si(\一位全加器fa封装2_69_si ), .Cin(undriven_78), .Xi(undriven_76),
    .Yi(undriven_77));
  shape shape_6 ();
  \一位全加器FA封装2  \u_一位全加器fa封装2_70  (
    .Cout(\一位全加器fa封装2_70_cout [0]), .Si(\一位全加器fa封装2_70_si ), .Cin(1'b0), .Xi(undriven_79), .Yi(undriven_80));
  \一位全加器FA封装2  \u_一位全加器fa封装2_71  (
    .Cout(\一位全加器fa封装2_71_cout ), .Si(\一位全加器fa封装2_71_si ), .Cin(\一位全加器fa封装2_78_cout [0]),
    .Xi(\一位全加器fa封装2_72_si ), .Yi(\一位全加器fa封装2_78_cout [1]));
  \一位全加器FA封装2  \u_一位全加器fa封装2_72  (
    .Cout(\一位全加器fa封装2_72_cout [0]), .Si(\一位全加器fa封装2_72_si ), .Cin(\一位全加器fa封装2_79_cout ),
    .Xi(\一位全加器fa封装2_73_si ), .Yi(\一位全加器fa封装2_76_si ));
  \一位全加器FA封装2  \u_一位全加器fa封装2_73  (
    .Cout(\一位全加器fa封装2_73_cout ), .Si(\一位全加器fa封装2_73_si ), .Cin(\一位全加器fa封装2_77_si ), .Xi(\一位全加器fa封装2_75_si ),
    .Yi(\一位全加器fa封装2_74_si ));
  \一位全加器FA封装2  \u_一位全加器fa封装2_74  (
    .Cout(\一位全加器fa封装2_77_cout [1]), .Si(\一位全加器fa封装2_74_si ), .Cin(undriven_86), .Xi(undriven_84),
    .Yi(undriven_85));
  \一位全加器FA封装2  \u_一位全加器fa封装2_75  (
    .Cout(\一位全加器fa封装2_77_cout [2]), .Si(\一位全加器fa封装2_75_si ), .Cin(undriven_83), .Xi(undriven_81),
    .Yi(undriven_82));
  \一位全加器FA封装2  \u_一位全加器fa封装2_76  (
    .Cout(\一位全加器fa封装2_72_cout [1]), .Si(\一位全加器fa封装2_76_si ), .Cin(\一位全加器fa封装2_83_cout [0]),
    .Xi(\一位全加器fa封装2_83_cout [2]), .Yi(\一位全加器fa封装2_83_cout [1]));
  \一位全加器FA封装2  \u_一位全加器fa封装2_77  (
    .Cout(\一位全加器fa封装2_77_cout [0]), .Si(\一位全加器fa封装2_77_si ), .Cin(1'b0), .Xi(undriven_87), .Yi(undriven_88));
  \一位全加器FA封装2  \u_一位全加器fa封装2_78  (
    .Cout(\一位全加器fa封装2_78_cout [0]), .Si(\一位全加器fa封装2_78_si ), .Cin(\一位全加器fa封装2_85_cout ),
    .Xi(\一位全加器fa封装2_79_si ), .Yi(\一位全加器fa封装2_82_si ));
  \一位全加器FA封装2  \u_一位全加器fa封装2_79  (
    .Cout(\一位全加器fa封装2_79_cout ), .Si(\一位全加器fa封装2_79_si ), .Cin(\一位全加器fa封装2_83_si ), .Xi(\一位全加器fa封装2_80_si ),
    .Yi(\一位全加器fa封装2_84_si ));
  \一位全加器FA封装2  \u_一位全加器fa封装2_80  (
    .Cout(\一位全加器fa封装2_83_cout [2]), .Si(\一位全加器fa封装2_80_si ), .Cin(undriven_91), .Xi(undriven_89),
    .Yi(undriven_90));
  shape shape_7 ();
  \一位全加器FA封装2  \u_一位全加器fa封装2_81  (
    .Cout(\一位全加器fa封装2_81_cout ), .Si(\一位全加器fa封装2_81_si ), .Cin(\一位全加器fa封装2_88_cout [0]),
    .Xi(\一位全加器fa封装2_78_si ), .Yi(\一位全加器fa封装2_88_cout [1]));
  \一位全加器FA封装2  \u_一位全加器fa封装2_82  (
    .Cout(\一位全加器fa封装2_78_cout [1]), .Si(\一位全加器fa封装2_82_si ), .Cin(\一位全加器fa封装2_90_cout [0]),
    .Xi(\一位全加器fa封装2_90_cout [2]), .Yi(\一位全加器fa封装2_90_cout [1]));
  \一位全加器FA封装2  \u_一位全加器fa封装2_83  (
    .Cout(\一位全加器fa封装2_83_cout [0]), .Si(\一位全加器fa封装2_83_si ), .Cin(1'b0), .Xi(undriven_95), .Yi(undriven_96));
  \一位全加器FA封装2  \u_一位全加器fa封装2_84  (
    .Cout(\一位全加器fa封装2_83_cout [1]), .Si(\一位全加器fa封装2_84_si ), .Cin(undriven_94), .Xi(undriven_92),
    .Yi(undriven_93));
  \一位全加器FA封装2  \u_一位全加器fa封装2_85  (
    .Cout(\一位全加器fa封装2_85_cout ), .Si(\一位全加器fa封装2_85_si ), .Cin(\一位全加器fa封装2_90_si ), .Xi(\一位全加器fa封装2_86_si ),
    .Yi(\一位全加器fa封装2_91_si ));
  \一位全加器FA封装2  \u_一位全加器fa封装2_86  (
    .Cout(\一位全加器fa封装2_90_cout [2]), .Si(\一位全加器fa封装2_86_si ), .Cin(undriven_99), .Xi(undriven_97),
    .Yi(undriven_98));
  \一位全加器FA封装2  \u_一位全加器fa封装2_87  (
    .Cout(\一位全加器fa封装2_87_cout ), .Si(\一位全加器fa封装2_87_si ), .Cin(\一位全加器fa封装2_94_cout [0]),
    .Xi(\一位全加器fa封装2_88_si ), .Yi(\一位全加器fa封装2_94_cout [1]));
  \一位全加器FA封装2  \u_一位全加器fa封装2_88  (
    .Cout(\一位全加器fa封装2_88_cout [0]), .Si(\一位全加器fa封装2_88_si ), .Cin(\一位全加器fa封装2_96_cout ),
    .Xi(\一位全加器fa封装2_85_si ), .Yi(\一位全加器fa封装2_89_si ));
  \一位全加器FA封装2  \u_一位全加器fa封装2_89  (
    .Cout(\一位全加器fa封装2_88_cout [1]), .Si(\一位全加器fa封装2_89_si ), .Cin(\一位全加器fa封装2_98_cout [0]),
    .Xi(\一位全加器fa封装2_98_cout [2]), .Yi(\一位全加器fa封装2_98_cout [1]));
  \一位全加器FA封装2  \u_一位全加器fa封装2_90  (
    .Cout(\一位全加器fa封装2_90_cout [0]), .Si(\一位全加器fa封装2_90_si ), .Cin(1'b0), .Xi(undriven_103), .Yi(undriven_104));
  \一位全加器FA封装2  \u_一位全加器fa封装2_91  (
    .Cout(\一位全加器fa封装2_90_cout [1]), .Si(\一位全加器fa封装2_91_si ), .Cin(undriven_102), .Xi(undriven_100),
    .Yi(undriven_101));
  \一位全加器FA封装2  \u_一位全加器fa封装2_92  (
    .Cout(\一位全加器fa封装2_98_cout [2]), .Si(\一位全加器fa封装2_92_si ), .Cin(undriven_107), .Xi(undriven_105),
    .Yi(undriven_106));
  \一位全加器FA封装2  \u_一位全加器fa封装2_93  (
    .Cout(\一位全加器fa封装2_93_cout ), .Si(\一位全加器fa封装2_93_si ), .Cin(\一位全加器fa封装2_100_cout [0]),
    .Xi(\一位全加器fa封装2_94_si ), .Yi(\一位全加器fa封装2_100_cout [1]));
  \一位全加器FA封装2  \u_一位全加器fa封装2_94  (
    .Cout(\一位全加器fa封装2_94_cout [0]), .Si(\一位全加器fa封装2_94_si ), .Cin(\一位全加器fa封装2_101_cout ),
    .Xi(\一位全加器fa封装2_96_si ), .Yi(\一位全加器fa封装2_95_si ));
  \一位全加器FA封装2  \u_一位全加器fa封装2_95  (
    .Cout(\一位全加器fa封装2_94_cout [1]), .Si(\一位全加器fa封装2_95_si ), .Cin(\一位全加器fa封装2_105_cout [0]),
    .Xi(\一位全加器fa封装2_105_cout [2]), .Yi(\一位全加器fa封装2_105_cout [1]));
  \一位全加器FA封装2  \u_一位全加器fa封装2_96  (
    .Cout(\一位全加器fa封装2_96_cout ), .Si(\一位全加器fa封装2_96_si ), .Cin(\一位全加器fa封装2_98_si ), .Xi(\一位全加器fa封装2_92_si ),
    .Yi(\一位全加器fa封装2_97_si ));
  \一位全加器FA封装2  \u_一位全加器fa封装2_97  (
    .Cout(\一位全加器fa封装2_98_cout [1]), .Si(\一位全加器fa封装2_97_si ), .Cin(undriven_110), .Xi(undriven_108),
    .Yi(undriven_109));
  shape shape_8 ();
  \一位全加器FA封装2  \u_一位全加器fa封装2_98  (
    .Cout(\一位全加器fa封装2_98_cout [0]), .Si(\一位全加器fa封装2_98_si ), .Cin(1'b0), .Xi(undriven_111), .Yi(undriven_112));
  \一位全加器FA封装2  \u_一位全加器fa封装2_99  (
    .Cout(\一位全加器fa封装2_99_cout ), .Si(\一位全加器fa封装2_99_si ), .Cin(\一位全加器fa封装2_106_cout [0]),
    .Xi(\一位全加器fa封装2_100_si ), .Yi(\一位全加器fa封装2_106_cout [1]));
  \一位全加器FA封装2  \u_一位全加器fa封装2_100  (
    .Cout(\一位全加器fa封装2_100_cout [0]), .Si(\一位全加器fa封装2_100_si ), .Cin(\一位全加器fa封装2_107_cout ),
    .Xi(\一位全加器fa封装2_101_si ), .Yi(\一位全加器fa封装2_104_si ));
  \一位全加器FA封装2  \u_一位全加器fa封装2_101  (
    .Cout(\一位全加器fa封装2_101_cout ), .Si(\一位全加器fa封装2_101_si ), .Cin(\一位全加器fa封装2_105_si ),
    .Xi(\一位全加器fa封装2_102_si ), .Yi(\一位全加器fa封装2_103_si ));
  \一位全加器FA封装2  \u_一位全加器fa封装2_102  (
    .Cout(\一位全加器fa封装2_105_cout [2]), .Si(\一位全加器fa封装2_102_si ), .Cin(undriven_115), .Xi(undriven_113),
    .Yi(undriven_114));
  \一位全加器FA封装2  \u_一位全加器fa封装2_103  (
    .Cout(\一位全加器fa封装2_105_cout [1]), .Si(\一位全加器fa封装2_103_si ), .Cin(undriven_118), .Xi(undriven_116),
    .Yi(undriven_117));
  \一位全加器FA封装2  \u_一位全加器fa封装2_104  (
    .Cout(\一位全加器fa封装2_100_cout [1]), .Si(\一位全加器fa封装2_104_si ), .Cin(\一位全加器fa封装2_111_cout [0]),
    .Xi(\一位全加器fa封装2_111_cout [2]), .Yi(\一位全加器fa封装2_111_cout [1]));
  \一位全加器FA封装2  \u_一位全加器fa封装2_105  (
    .Cout(\一位全加器fa封装2_105_cout [0]), .Si(\一位全加器fa封装2_105_si ), .Cin(1'b0), .Xi(undriven_119),
    .Yi(undriven_120));
  \一位全加器FA封装2  \u_一位全加器fa封装2_106  (
    .Cout(\一位全加器fa封装2_106_cout [0]), .Si(\一位全加器fa封装2_106_si ), .Cin(undriven_125), .Xi(\一位全加器fa封装2_107_si ),
    .Yi(\一位全加器fa封装2_110_si ));
  \一位全加器FA封装2  \u_一位全加器fa封装2_107  (
    .Cout(\一位全加器fa封装2_107_cout ), .Si(\一位全加器fa封装2_107_si ), .Cin(\一位全加器fa封装2_111_si ),
    .Xi(\一位全加器fa封装2_108_si ), .Yi(\一位全加器fa封装2_112_si ));
  \一位全加器FA封装2  \u_一位全加器fa封装2_108  (
    .Cout(\一位全加器fa封装2_111_cout [2]), .Si(\一位全加器fa封装2_108_si ), .Cin(undriven_123), .Xi(undriven_121),
    .Yi(undriven_122));
  \一位全加器FA封装2  \u_一位全加器fa封装2_109  (
    .Cout(\一位全加器fa封装2_109_cout ), .Si(\一位全加器fa封装2_109_si ), .Cin(undriven_131[0]), .Xi(\一位全加器fa封装2_106_si ),
    .Yi(undriven_131[1]));
  \一位全加器FA封装2  \u_一位全加器fa封装2_110  (
    .Cout(\一位全加器fa封装2_106_cout [1]), .Si(\一位全加器fa封装2_110_si ), .Cin(undriven_129[0]), .Xi(undriven_129[2]),
    .Yi(undriven_129[1]));
  \一位全加器FA封装2  \u_一位全加器fa封装2_111  (
    .Cout(\一位全加器fa封装2_111_cout [0]), .Si(\一位全加器fa封装2_111_si ), .Cin(1'b0), .Xi(undriven_128),
    .Yi(undriven_130));
  \一位全加器FA封装2  \u_一位全加器fa封装2_112  (
    .Cout(\一位全加器fa封装2_111_cout [1]), .Si(\一位全加器fa封装2_112_si ), .Cin(undriven_127), .Xi(undriven_124),
    .Yi(undriven_126));
endmodule

// Trace
module trace (
  input  [7:0] in_1,
  output [31:0] X,
  output [31:0] Y,
  output [3:0] AluOP,
  output [31:0] R,
  output [31:0] R2,
  output [2:0] FLAGS
);

  ROM #(.dataWidth(32)) rom_1 (.addr(in_1), .data(X));  // open: sel
  ROM #(.dataWidth(32)) rom_2 (.addr(in_1), .data(Y));  // open: sel
  ROM #(.dataWidth(4)) rom_3 (.addr(in_1), .data(AluOP));  // open: sel
  ROM #(.dataWidth(32)) rom_4 (.addr(in_1), .data(R));  // open: sel
  ROM #(.dataWidth(32)) rom_5 (.addr(in_1), .data(R2));  // open: sel
  ROM #(.dataWidth(3)) rom_6 (.addr(in_1), .data(FLAGS));  // open: sel

  // Notes on the sheet:
  //   X trace
  //   Y trace
  //   ALU OP Trace
  //   Result Benchmark
  //   Result2 Benchmark
  //   FLAGS Benchmark
  //   contents of rom_1 (hex, n*v repeats v):
  //   ff00ffff ff00ffff ff000000 ff00ffff 7fffffff fffffffe ffff ffffffff 7fffffff 80000000 7ff00000 7c
  //   80000000 7fffffff ff00ffff 7fffffff 18*fffffffe
  //   contents of rom_2 (hex, n*v repeats v):
  //   7 ff00ffff 18 18 10 10 80 ffffffff c 80000000 7c 7ff00000 1 fffffffe 18 74 fffffffe 88 10 ffffffff
  //   10 ffffffff 12*10
  //   contents of rom_3 (hex, n*v repeats v):
  //   0 0 1 2 3 4 4*5 4*6 7 8 9 a b b c c f 11*9 f
  //   contents of rom_4 (hex, n*v repeats v):
  //   807fff80 80000000 ffffffff ff fffffff0 fffffff 1007f fffffffe 8000000b 0 7fefff84 8010007c 7fffffff
  //   80000001 18 7fffffff 0 1 1 1 0 1 300000 11*ffffffee 1
  //   contents of rom_5 (hex, n*v repeats v):
  //   4*0 7 e
  //   contents of rom_6 (hex, n*v repeats v):
  //   0 1 5*0 3 4 7 0 2 4 6 0 0 1 17*0 66*1
endmodule

// 单项评分
module \单项评分  (
  input  ALU_SWITCH,
  input  EQ,
  input  EN,
  input  [4:0] \分值 ,
  input  CLK,
  output [7:0] \正确条数 ,
  output [7:0] \扣分 ,
  output Right,
  output [7:0] Total
);

  wire and_1_out, and_2_out, not_1_out, priority_encoder_1_gs, priority_encoder_1_out;
  wire [7:0] bit_extender_1_out;

  and and_1 (and_1_out, ALU_SWITCH, EN);
  Priority_Encoder #(.select(1)) priority_encoder_1 (
    .in0(EQ), .in1(EQ), .out(priority_encoder_1_out), .gs(priority_encoder_1_gs));  // open: en_out, en_in
  Counter counter_1 (.count(and_1_out), .Q(Total), .clk(CLK));  // open: load, D, carry, clr
  and and_2 (and_2_out, ALU_SWITCH, priority_encoder_1_out, priority_encoder_1_gs, EN);
  Counter counter_2 (.count(and_2_out), .Q(\正确条数 ), .clk(CLK));  // open: load, D, carry, clr
  Comparator comparator_1 (.a(\正确条数 ), .b(Total), .eq(Right));  // open: gt, lt
  assign bit_extender_1_out = {{3{1'b0}}, \分值 };  // Bit_Extender bit_extender_1
  Multiplexer #(.width(8), .enable("false")) multiplexer_1 (
    .in0({8{1'b0}}), .in1(bit_extender_1_out), .out(\扣分 ), .sel(not_1_out));
  not not_1 (not_1_out, Right);

  // Notes on the sheet:
  //   只有使用优先编码器才能屏蔽掉位置状态
endmodule

module \总评分  (
  input  [7:0] in_1,
  input  [7:0] in_2,
  input  [7:0] in_3,
  input  [7:0] in_4,
  input  [7:0] in_5,
  input  [7:0] in_6,
  input  [7:0] in_7,
  input  [7:0] in_8,
  input  [7:0] in_9,
  input  [7:0] in_10,
  input  [7:0] in_11,
  input  [7:0] in_12,
  input  [7:0] in_13,
  input  [7:0] in_14,
  input  [7:0] in_15,
  input  [7:0] in_16,
  input  \悬空扣分 ,
  output [7:0] Result,
  output [3:0] High,
  output [3:0] Low,
  output [3:0] Mid
);

  wire [7:0] adder_1_out, adder_2_out, adder_3_out, adder_4_out, adder_5_out, adder_6_out, adder_7_out,
       adder_8_out, adder_9_out, adder_10_out, adder_11_out, adder_12_out, adder_13_out, adder_14_out,
       adder_15_out, divider_1_out, subtractor_1_out, subtractor_2_out;
  wire [7:4] divider_1_rem, divider_2_out, divider_2_rem;

  Adder adder_1 (.a(in_1), .b(in_2), .out(adder_1_out));  // open: cin, cout
  Adder adder_2 (.a(in_3), .b(in_4), .out(adder_2_out));  // open: cin, cout
  Adder adder_3 (.a(in_5), .b(in_6), .out(adder_3_out));  // open: cin, cout
  Adder adder_4 (.a(in_7), .b(in_8), .out(adder_4_out));  // open: cin, cout
  Adder adder_5 (.a(in_9), .b(in_10), .out(adder_5_out));  // open: cin, cout
  Adder adder_6 (.a(in_11), .b(in_12), .out(adder_6_out));  // open: cin, cout
  Adder adder_7 (.a(in_13), .b(in_14), .out(adder_7_out));  // open: cin, cout
  Adder adder_8 (.a(in_15), .b(in_16), .out(adder_8_out));  // open: cin, cout
  Adder adder_9 (.a(adder_1_out), .b(adder_2_out), .out(adder_9_out));  // open: cin, cout
  Adder adder_10 (.a(adder_3_out), .b(adder_4_out), .out(adder_10_out));  // open: cin, cout
  Adder adder_11 (.a(adder_5_out), .b(adder_6_out), .out(adder_11_out));  // open: cin, cout
  Adder adder_12 (.a(adder_7_out), .b(adder_8_out), .out(adder_12_out));  // open: cin, cout
  Adder adder_13 (.a(adder_9_out), .b(adder_10_out), .out(adder_13_out));  // open: cin, cout
  Adder adder_14 (.a(adder_11_out), .b(adder_12_out), .out(adder_14_out));  // open: cin, cout
  Adder adder_15 (.a(adder_13_out), .b(adder_14_out), .out(adder_15_out));  // open: cin, cout
  Subtractor subtractor_1 (.a(8'h64), .b(adder_15_out), .out(subtractor_1_out));  // open: bin, bout
  Subtractor subtractor_2 (.a(subtractor_1_out), .b(8'h5), .out(subtractor_2_out));  // open: bin, bout
  Multiplexer #(.width(8), .enable("false")) multiplexer_1 (
    .in0(subtractor_1_out), .in1(subtractor_2_out), .out(Result), .sel(\悬空扣分 ));
  Divider divider_1 (.a(Result), .b(8'ha), .out(divider_1_out), .rem({divider_1_rem, Low}));  // open: upper
  Divider divider_2 (
    .a(divider_1_out), .b(8'ha), .out({divider_2_out, High}), .rem({divider_2_rem, Mid}));  // open: upper
endmodule

module \四位并行加法器  (
  input  C0,
  input  A1,
  input  B1,
  input  A2,
  input  B2,
  input  A3,
  input  B3,
  input  A4,
  input  B4,
  output S1,
  output S2,
  output S3,
  output S4,
  output \进位C 
);

  wire A1_t, A2_t, A3_t, A4_t, and_1_out, and_2_out, and_3_out, and_4_out, and_5_out, and_6_out, and_7_out,
       and_8_out, and_9_out, and_10_out, and_11_out, and_12_out, and_13_out, and_14_out, and_15_out,
       and_16_out, and_17_out, and_18_out, C1_out, C2_out, C3_out, Cin, X1, X2, X3, X4, xor_1_out, xor_2_out,
       xor_3_out, xor_4_out, \进位4 ;

  xor xor_1 (xor_1_out, A1, B1);
  xor xor_2 (xor_2_out, A2, B2);
  xor xor_3 (xor_3_out, A3, B3);
  xor xor_4 (xor_4_out, A4, B4);
  and and_1 (and_1_out, xor_1_out, C0);
  and and_2 (and_2_out, xor_1_out, xor_2_out, C0);
  and and_3 (and_3_out, C0, xor_3_out, xor_1_out, xor_3_out);
  and and_4 (and_4_out, C0, xor_3_out, xor_4_out, xor_1_out, xor_2_out);
  and and_5 (and_5_out, A1, B1);
  and and_6 (and_6_out, A1, B1, xor_2_out);
  and and_7 (and_7_out, A2, B2);
  and and_8 (and_8_out, A1, B1, xor_2_out, xor_3_out);
  and and_9 (and_9_out, A2, B2, xor_3_out);
  and and_10 (and_10_out, A3, B3);
  and and_11 (and_11_out, A1, B1, xor_2_out, xor_3_out, xor_4_out);
  and and_12 (and_12_out, A2, B2, xor_3_out, xor_4_out);
  and and_13 (and_13_out, A3, B3, xor_4_out);
  and and_14 (and_14_out, A4, B4);
  or C1 (C1_out, and_1_out, and_5_out);
  or C2 (C2_out, and_2_out, and_6_out, and_7_out);
  or C3 (C3_out, and_3_out, and_8_out, and_9_out, and_10_out);
  or C4 (\进位C , and_4_out, and_11_out, and_12_out, and_13_out, and_14_out);
  xor xor_5 (S1, C0, xor_1_out);
  xor xor_6 (S2, C1_out, xor_2_out);
  xor xor_7 (S3, C2_out, xor_3_out);
  xor xor_8 (S4, C3_out, xor_4_out);
  and and_15 (and_15_out, X1, Cin, X2, X4, X3);
  and and_16 (and_16_out, X2, X3, X4, A1_t);
  and and_17 (and_17_out, X3, X4, A2_t);
  and and_18 (and_18_out, X4, A3_t);
  or or_1 (\进位4 , and_15_out, and_16_out, and_17_out, and_18_out, A4_t);
endmodule

module \有符号减法溢出表达式生成  (
  input  x,
  input  s,
  input  y,
  output z
);

  wire and_1_out, and_2_out, not_1_out, not_2_out, not_3_out;

  not not_1 (not_1_out, x);
  not not_2 (not_2_out, s);
  not not_3 (not_3_out, y);
  and and_1 (and_1_out, not_1_out, s, y);
  and and_2 (and_2_out, x, not_2_out, not_3_out);
  or or_1 (z, and_1_out, and_2_out);
endmodule
